// Logisim project xcm.circ as structural Verilog: 25 circuits, main circuit main
module main (
);

  wire clock_1_out;
  wire [1:0] joystick_1_y, joystick_2_y;
  wire [2:0] undriven, undriven_2;
  wire [9:0] xcm_cpu_1_ir_adr;
  wire [11:0] xcm_cpu_1_display;
  wire [14:0] rom_1_data;
  wire [31:0] mm10_1_r00, mm10_1_r0a, mm10_1_r0b, mm10_1_r0c, mm10_1_r0d, mm10_1_r0e, mm10_1_r0f, mm10_1_r01,
       mm10_1_r1a, mm10_1_r1b, mm10_1_r1c, mm10_1_r1d, mm10_1_r1e, mm10_1_r1f, mm10_1_r02, mm10_1_r03,
       mm10_1_r04, mm10_1_r05, mm10_1_r06, mm10_1_r07, mm10_1_r08, mm10_1_r09, mm10_1_r10, mm10_1_r11,
       mm10_1_r12, mm10_1_r13, mm10_1_r14, mm10_1_r15, mm10_1_r16, mm10_1_r17, mm10_1_r18, mm10_1_r19;

  Clock clock_1 (.out(clock_1_out));
  XCM_CPU xcm_cpu_1 (
    .CLK(clock_1_out), .IR_DATA(rom_1_data), .INPUT_0({undriven, joystick_1_y}),
    .INPUT_1({undriven_2, joystick_2_y}), .DISPLAY(xcm_cpu_1_display), .IR_ADR(xcm_cpu_1_ir_adr));  // open: INPUT_2, INPUT_3
  ROM #(.addrWidth(10), .dataWidth(15)) rom_1 (.addr(xcm_cpu_1_ir_adr), .data(rom_1_data));  // open: sel
  MM10 mm10_1 (
    .SEL(xcm_cpu_1_display[0]), .P(xcm_cpu_1_display[1]), .R00(mm10_1_r00), .R01(mm10_1_r01),
    .R02(mm10_1_r02), .R03(mm10_1_r03), .R04(mm10_1_r04), .R05(mm10_1_r05), .R06(mm10_1_r06),
    .R07(mm10_1_r07), .R08(mm10_1_r08), .R09(mm10_1_r09), .R0A(mm10_1_r0a), .R0B(mm10_1_r0b),
    .R0C(mm10_1_r0c), .R0D(mm10_1_r0d), .R0E(mm10_1_r0e), .R0F(mm10_1_r0f), .R10(mm10_1_r10),
    .R11(mm10_1_r11), .R12(mm10_1_r12), .R13(mm10_1_r13), .R14(mm10_1_r14), .R15(mm10_1_r15),
    .R16(mm10_1_r16), .R17(mm10_1_r17), .R18(mm10_1_r18), .R19(mm10_1_r19), .R1A(mm10_1_r1a),
    .R1B(mm10_1_r1b), .R1C(mm10_1_r1c), .R1D(mm10_1_r1d), .R1E(mm10_1_r1e), .R1F(mm10_1_r1f),
    .CLK(clock_1_out), .Y(xcm_cpu_1_display[11:7]), .X(xcm_cpu_1_display[6:2]));
  DotMatrix #(.inputtype("row"), .matrixcols(32), .matrixrows(32), .persist(1)) dotmatrix_1 (
    .row0(mm10_1_r00), .row1(mm10_1_r01), .row2(mm10_1_r02), .row3(mm10_1_r03), .row4(mm10_1_r04),
    .row5(mm10_1_r05), .row6(mm10_1_r06), .row7(mm10_1_r07), .row8(mm10_1_r08), .row9(mm10_1_r09),
    .row10(mm10_1_r0a), .row11(mm10_1_r0b), .row12(mm10_1_r0c), .row13(mm10_1_r0d), .row14(mm10_1_r0e),
    .row15(mm10_1_r0f), .row16(mm10_1_r10), .row17(mm10_1_r11), .row18(mm10_1_r12), .row19(mm10_1_r13),
    .row20(mm10_1_r14), .row21(mm10_1_r15), .row22(mm10_1_r16), .row23(mm10_1_r17), .row24(mm10_1_r18),
    .row25(mm10_1_r19), .row26(mm10_1_r1a), .row27(mm10_1_r1b), .row28(mm10_1_r1c), .row29(mm10_1_r1d),
    .row30(mm10_1_r1e), .row31(mm10_1_r1f));
  Joystick #(.bits(2)) joystick_1 (.y(joystick_1_y));  // open: x
  Joystick #(.bits(2)) joystick_2 (.y(joystick_2_y));  // open: x
  Button button_1 ();  // open: out

  // Notes on the sheet:
  //   contents of rom_1 (hex, n*v repeats v):
  //   30c8 34c8 38c8 3cc8 40c8 44c8 48c8 30e8 3ce8 3108 3d08 3528 3928 3d28 3168 3568 3968 3d68 4168 4568
  //   4968 3188 4988 31a8 49a8 31c8 35c8 39c8 3dc8 41c8 45c8 49c8 3208 3608 3a08 3e08 4208 4608 4a08 3a28
  //   3e48 4268 3288 3688 3a88 3e88 4288 4688 4a88 32c8 36c8 3ac8 3ec8 42c8 46c8 4ac8 32e8 4ae8 3308 3f08
  //   4b08 3328 3f28 4328 4728 4b28 7c01 940 5 1421 840 25 8a0 840 30ca 34ca 38ca 3cca 40ca 44ca 48ca 30ea
  //   3cea 310a 3d0a 352a 392a 3d2a 316a 356a 396a 3d6a 416a 456a 496a 318a 498a 31aa 49aa 31ca 35ca 39ca
  //   3dca 41ca 45ca 49ca 320a 360a 3a0a 3e0a 420a 460a 4a0a 3a2a 3e4a 426a 328a 368a 3a8a 3e8a 428a 468a
  //   4a8a 32ca 36ca 3aca 3eca 42ca 46ca 4aca 32ea 4aea 330a 3f0a 4b0a 332a 3f2a 432a 472a 4b2a 1520 c49
  //   403 4a4 25 25 83 407 804 c24 7d63 165 7d61 14a0 2d60 c49 7803 4c4 25 25 c83 407 804 c24 7d63 165
  //   7d61 14a0 2d60 2803 4023 2843 4063 83 38a3 38c3 123 28a4 2927 145 2927 145 2927 145 2927 145 7d23
  //   28c4 2927 145 2927 145 2927 145 2927 145 80c 1ca0 c0c 1960 40c 1ae0 1ca0 70a1 1ca0 123 28a4 2929 a5
  //   4*145 2927 1ca0 a1 1ca0 a6 123 28a4 2927 4*145 2929 1ca0 82c 2040 c2c 1d40 42c 1ec0 2040 70c1 2040
  //   7d23 28c4 2929 c5 4*145 2927 2040 c1 2040 c6 7d23 28c4 2927 4*145 2929 2040 81 21c0 481 2220 881
  //   22e0 c81 2280 1081 2340 1481 2380 5 25 23c0 5 26 23c0 6 25 23c0 6 26 23c0 6 23c0 5 23c0 7c21 2820 21
  //   28c0 401 24e0 7801 2680 2d60 28a4 282e 2b20 145 282e 2ce0 145 282e 2ce0 145 282e 2c00 1360 28c4 282e
  //   2960 145 282e 2d20 145 282e 2d20 145 282e 2a40 11a0 81 483 c81 883 2d60 481 83 881 c83 2d60 81 c83
  //   481 883 1481 883 2d60 81 c83 481 883 1481 c83 2d60 c81 83 881 483 1081 483 2d60 c81 83 881 483 1081
  //   83 2d60 1483 2d60 1083 2d60 407 c49 804 c24 1880
endmodule

module MemRow2 (
  input  CLK,
  input  SEL,
  input  ADR_0,
  input  ADR_1,
  input  P,
  output M00,
  output M01,
  output M10,
  output M11
);

  wire demultiplexer_1_out0, demultiplexer_1_out1, demultiplexer_2_out0, demultiplexer_2_out1,
       demultiplexer_3_out0, demultiplexer_3_out1, demultiplexer_4_out0, demultiplexer_4_out1,
       demultiplexer_5_out0, demultiplexer_5_out1, demultiplexer_6_out0, demultiplexer_6_out1,
       demultiplexer_7_out0, demultiplexer_7_out1;

  Demultiplexer demultiplexer_1 (
    .out0(demultiplexer_1_out0), .out1(demultiplexer_1_out1), .in(SEL), .sel(ADR_0));  // open: en
  Demultiplexer demultiplexer_2 (
    .out0(demultiplexer_2_out0), .out1(demultiplexer_2_out1), .in(demultiplexer_1_out0), .sel(ADR_1));  // open: en
  Demultiplexer demultiplexer_3 (
    .out0(demultiplexer_3_out0), .out1(demultiplexer_3_out1), .in(demultiplexer_1_out1), .sel(ADR_1));  // open: en
  Demultiplexer demultiplexer_4 (
    .out0(demultiplexer_4_out0), .out1(demultiplexer_4_out1), .in(demultiplexer_2_out0), .sel(P));  // open: en
  Demultiplexer demultiplexer_5 (
    .out0(demultiplexer_5_out0), .out1(demultiplexer_5_out1), .in(demultiplexer_2_out1), .sel(P));  // open: en
  Demultiplexer demultiplexer_6 (
    .out0(demultiplexer_6_out0), .out1(demultiplexer_6_out1), .in(demultiplexer_3_out0), .sel(P));  // open: en
  Demultiplexer demultiplexer_7 (
    .out0(demultiplexer_7_out0), .out1(demultiplexer_7_out1), .in(demultiplexer_3_out1), .sel(P));  // open: en
  S_R_Flip_Flop _00 (
    .S(demultiplexer_4_out1), .clk(CLK), .R(demultiplexer_4_out0), .Q(M00));  // open: Qn, preset, reset, en
  S_R_Flip_Flop _01 (
    .S(demultiplexer_5_out1), .clk(CLK), .R(demultiplexer_5_out0), .Q(M01));  // open: Qn, preset, reset, en
  S_R_Flip_Flop _10 (
    .S(demultiplexer_6_out1), .clk(CLK), .R(demultiplexer_6_out0), .Q(M10));  // open: Qn, preset, reset, en
  S_R_Flip_Flop _11 (
    .S(demultiplexer_7_out1), .clk(CLK), .R(demultiplexer_7_out0), .Q(M11));  // open: Qn, preset, reset, en
endmodule

module MemRow5 (
  input  CLK,
  input  SEL,
  input  ADR_0,
  input  ADR_1,
  input  ADR_2,
  input  ADR_3,
  input  ADR_4,
  input  P,
  output [31:0] MEM
);

  wire demultiplexer_1_out0, demultiplexer_1_out1, demultiplexer_2_out0, demultiplexer_2_out1,
       demultiplexer_3_out0, demultiplexer_3_out1, demultiplexer_4_out0, demultiplexer_4_out1,
       demultiplexer_5_out0, demultiplexer_5_out1, demultiplexer_6_out0, demultiplexer_6_out1,
       demultiplexer_7_out0, demultiplexer_7_out1, demultiplexer_8_out0, demultiplexer_8_out1,
       demultiplexer_9_out0, demultiplexer_9_out1, demultiplexer_10_out0, demultiplexer_10_out1,
       demultiplexer_11_out0, demultiplexer_11_out1, demultiplexer_12_out0, demultiplexer_12_out1,
       demultiplexer_13_out0, demultiplexer_13_out1, demultiplexer_14_out0, demultiplexer_14_out1,
       demultiplexer_15_out0, demultiplexer_15_out1, demultiplexer_16_out0, demultiplexer_16_out1,
       demultiplexer_17_out0, demultiplexer_17_out1, demultiplexer_18_out0, demultiplexer_18_out1,
       demultiplexer_19_out0, demultiplexer_19_out1, demultiplexer_20_out0, demultiplexer_20_out1,
       demultiplexer_21_out0, demultiplexer_21_out1, demultiplexer_22_out0, demultiplexer_22_out1,
       demultiplexer_23_out0, demultiplexer_23_out1, demultiplexer_24_out0, demultiplexer_24_out1,
       demultiplexer_25_out0, demultiplexer_25_out1, demultiplexer_26_out0, demultiplexer_26_out1,
       demultiplexer_27_out0, demultiplexer_27_out1, demultiplexer_28_out0, demultiplexer_28_out1,
       demultiplexer_29_out0, demultiplexer_29_out1, demultiplexer_30_out0, demultiplexer_30_out1,
       demultiplexer_31_out0, demultiplexer_31_out1, demultiplexer_32_out0, demultiplexer_32_out1,
       demultiplexer_33_out0, demultiplexer_33_out1, demultiplexer_34_out0, demultiplexer_34_out1,
       demultiplexer_35_out0, demultiplexer_35_out1, demultiplexer_36_out0, demultiplexer_36_out1,
       demultiplexer_37_out0, demultiplexer_37_out1, demultiplexer_38_out0, demultiplexer_38_out1,
       demultiplexer_39_out0, demultiplexer_39_out1, demultiplexer_40_out0, demultiplexer_40_out1,
       demultiplexer_41_out0, demultiplexer_41_out1, demultiplexer_42_out0, demultiplexer_42_out1,
       demultiplexer_43_out0, demultiplexer_43_out1, demultiplexer_44_out0, demultiplexer_44_out1,
       demultiplexer_45_out0, demultiplexer_45_out1, demultiplexer_46_out0, demultiplexer_46_out1,
       demultiplexer_47_out0, demultiplexer_47_out1, demultiplexer_48_out0, demultiplexer_48_out1,
       demultiplexer_49_out0, demultiplexer_49_out1, demultiplexer_50_out0, demultiplexer_50_out1,
       demultiplexer_51_out0, demultiplexer_51_out1, demultiplexer_52_out0, demultiplexer_52_out1,
       demultiplexer_53_out0, demultiplexer_53_out1, demultiplexer_54_out0, demultiplexer_54_out1,
       demultiplexer_55_out0, demultiplexer_55_out1, demultiplexer_56_out0, demultiplexer_56_out1,
       demultiplexer_57_out0, demultiplexer_57_out1, demultiplexer_58_out0, demultiplexer_58_out1,
       demultiplexer_59_out0, demultiplexer_59_out1, demultiplexer_60_out0, demultiplexer_60_out1,
       demultiplexer_61_out0, demultiplexer_61_out1, demultiplexer_62_out0, demultiplexer_62_out1,
       demultiplexer_63_out0, demultiplexer_63_out1;

  Demultiplexer demultiplexer_1 (
    .out0(demultiplexer_1_out0), .out1(demultiplexer_1_out1), .in(SEL), .sel(ADR_0));  // open: en
  Demultiplexer demultiplexer_2 (
    .out0(demultiplexer_2_out0), .out1(demultiplexer_2_out1), .in(demultiplexer_1_out0), .sel(ADR_1));  // open: en
  Demultiplexer demultiplexer_3 (
    .out0(demultiplexer_3_out0), .out1(demultiplexer_3_out1), .in(demultiplexer_1_out1), .sel(ADR_1));  // open: en
  Demultiplexer demultiplexer_4 (
    .out0(demultiplexer_4_out0), .out1(demultiplexer_4_out1), .in(demultiplexer_2_out0), .sel(ADR_2));  // open: en
  Demultiplexer demultiplexer_5 (
    .out0(demultiplexer_5_out0), .out1(demultiplexer_5_out1), .in(demultiplexer_2_out1), .sel(ADR_2));  // open: en
  Demultiplexer demultiplexer_6 (
    .out0(demultiplexer_6_out0), .out1(demultiplexer_6_out1), .in(demultiplexer_3_out0), .sel(ADR_2));  // open: en
  Demultiplexer demultiplexer_7 (
    .out0(demultiplexer_7_out0), .out1(demultiplexer_7_out1), .in(demultiplexer_3_out1), .sel(ADR_2));  // open: en
  Demultiplexer demultiplexer_8 (
    .out0(demultiplexer_8_out0), .out1(demultiplexer_8_out1), .in(demultiplexer_4_out0), .sel(ADR_3));  // open: en
  Demultiplexer demultiplexer_9 (
    .out0(demultiplexer_9_out0), .out1(demultiplexer_9_out1), .in(demultiplexer_4_out1), .sel(ADR_3));  // open: en
  Demultiplexer demultiplexer_10 (
    .out0(demultiplexer_10_out0), .out1(demultiplexer_10_out1), .in(demultiplexer_5_out0), .sel(ADR_3));  // open: en
  Demultiplexer demultiplexer_11 (
    .out0(demultiplexer_11_out0), .out1(demultiplexer_11_out1), .in(demultiplexer_5_out1), .sel(ADR_3));  // open: en
  Demultiplexer demultiplexer_12 (
    .out0(demultiplexer_12_out0), .out1(demultiplexer_12_out1), .in(demultiplexer_6_out0), .sel(ADR_3));  // open: en
  Demultiplexer demultiplexer_13 (
    .out0(demultiplexer_13_out0), .out1(demultiplexer_13_out1), .in(demultiplexer_6_out1), .sel(ADR_3));  // open: en
  Demultiplexer demultiplexer_14 (
    .out0(demultiplexer_14_out0), .out1(demultiplexer_14_out1), .in(demultiplexer_7_out0), .sel(ADR_3));  // open: en
  Demultiplexer demultiplexer_15 (
    .out0(demultiplexer_15_out0), .out1(demultiplexer_15_out1), .in(demultiplexer_7_out1), .sel(ADR_3));  // open: en
  Demultiplexer demultiplexer_16 (
    .out0(demultiplexer_16_out0), .out1(demultiplexer_16_out1), .in(demultiplexer_8_out0), .sel(ADR_4));  // open: en
  Demultiplexer demultiplexer_17 (
    .out0(demultiplexer_17_out0), .out1(demultiplexer_17_out1), .in(demultiplexer_8_out1), .sel(ADR_4));  // open: en
  Demultiplexer demultiplexer_18 (
    .out0(demultiplexer_18_out0), .out1(demultiplexer_18_out1), .in(demultiplexer_9_out0), .sel(ADR_4));  // open: en
  Demultiplexer demultiplexer_19 (
    .out0(demultiplexer_19_out0), .out1(demultiplexer_19_out1), .in(demultiplexer_9_out1), .sel(ADR_4));  // open: en
  Demultiplexer demultiplexer_20 (
    .out0(demultiplexer_20_out0), .out1(demultiplexer_20_out1), .in(demultiplexer_10_out0), .sel(ADR_4));  // open: en
  Demultiplexer demultiplexer_21 (
    .out0(demultiplexer_21_out0), .out1(demultiplexer_21_out1), .in(demultiplexer_10_out1), .sel(ADR_4));  // open: en
  Demultiplexer demultiplexer_22 (
    .out0(demultiplexer_22_out0), .out1(demultiplexer_22_out1), .in(demultiplexer_11_out0), .sel(ADR_4));  // open: en
  Demultiplexer demultiplexer_23 (
    .out0(demultiplexer_23_out0), .out1(demultiplexer_23_out1), .in(demultiplexer_11_out1), .sel(ADR_4));  // open: en
  Demultiplexer demultiplexer_24 (
    .out0(demultiplexer_24_out0), .out1(demultiplexer_24_out1), .in(demultiplexer_12_out0), .sel(ADR_4));  // open: en
  Demultiplexer demultiplexer_25 (
    .out0(demultiplexer_25_out0), .out1(demultiplexer_25_out1), .in(demultiplexer_12_out1), .sel(ADR_4));  // open: en
  Demultiplexer demultiplexer_26 (
    .out0(demultiplexer_26_out0), .out1(demultiplexer_26_out1), .in(demultiplexer_13_out0), .sel(ADR_4));  // open: en
  Demultiplexer demultiplexer_27 (
    .out0(demultiplexer_27_out0), .out1(demultiplexer_27_out1), .in(demultiplexer_13_out1), .sel(ADR_4));  // open: en
  Demultiplexer demultiplexer_28 (
    .out0(demultiplexer_28_out0), .out1(demultiplexer_28_out1), .in(demultiplexer_14_out0), .sel(ADR_4));  // open: en
  Demultiplexer demultiplexer_29 (
    .out0(demultiplexer_29_out0), .out1(demultiplexer_29_out1), .in(demultiplexer_14_out1), .sel(ADR_4));  // open: en
  Demultiplexer demultiplexer_30 (
    .out0(demultiplexer_30_out0), .out1(demultiplexer_30_out1), .in(demultiplexer_15_out0), .sel(ADR_4));  // open: en
  Demultiplexer demultiplexer_31 (
    .out0(demultiplexer_31_out0), .out1(demultiplexer_31_out1), .in(demultiplexer_15_out1), .sel(ADR_4));  // open: en
  Demultiplexer demultiplexer_32 (
    .out0(demultiplexer_32_out0), .out1(demultiplexer_32_out1), .in(demultiplexer_16_out0), .sel(P));  // open: en
  Demultiplexer demultiplexer_33 (
    .out0(demultiplexer_33_out0), .out1(demultiplexer_33_out1), .in(demultiplexer_16_out1), .sel(P));  // open: en
  Demultiplexer demultiplexer_34 (
    .out0(demultiplexer_34_out0), .out1(demultiplexer_34_out1), .in(demultiplexer_17_out0), .sel(P));  // open: en
  Demultiplexer demultiplexer_35 (
    .out0(demultiplexer_35_out0), .out1(demultiplexer_35_out1), .in(demultiplexer_17_out1), .sel(P));  // open: en
  Demultiplexer demultiplexer_36 (
    .out0(demultiplexer_36_out0), .out1(demultiplexer_36_out1), .in(demultiplexer_18_out0), .sel(P));  // open: en
  Demultiplexer demultiplexer_37 (
    .out0(demultiplexer_37_out0), .out1(demultiplexer_37_out1), .in(demultiplexer_18_out1), .sel(P));  // open: en
  Demultiplexer demultiplexer_38 (
    .out0(demultiplexer_38_out0), .out1(demultiplexer_38_out1), .in(demultiplexer_19_out0), .sel(P));  // open: en
  Demultiplexer demultiplexer_39 (
    .out0(demultiplexer_39_out0), .out1(demultiplexer_39_out1), .in(demultiplexer_19_out1), .sel(P));  // open: en
  Demultiplexer demultiplexer_40 (
    .out0(demultiplexer_40_out0), .out1(demultiplexer_40_out1), .in(demultiplexer_20_out0), .sel(P));  // open: en
  Demultiplexer demultiplexer_41 (
    .out0(demultiplexer_41_out0), .out1(demultiplexer_41_out1), .in(demultiplexer_20_out1), .sel(P));  // open: en
  Demultiplexer demultiplexer_42 (
    .out0(demultiplexer_42_out0), .out1(demultiplexer_42_out1), .in(demultiplexer_21_out0), .sel(P));  // open: en
  Demultiplexer demultiplexer_43 (
    .out0(demultiplexer_43_out0), .out1(demultiplexer_43_out1), .in(demultiplexer_21_out1), .sel(P));  // open: en
  Demultiplexer demultiplexer_44 (
    .out0(demultiplexer_44_out0), .out1(demultiplexer_44_out1), .in(demultiplexer_22_out0), .sel(P));  // open: en
  Demultiplexer demultiplexer_45 (
    .out0(demultiplexer_45_out0), .out1(demultiplexer_45_out1), .in(demultiplexer_22_out1), .sel(P));  // open: en
  Demultiplexer demultiplexer_46 (
    .out0(demultiplexer_46_out0), .out1(demultiplexer_46_out1), .in(demultiplexer_23_out0), .sel(P));  // open: en
  Demultiplexer demultiplexer_47 (
    .out0(demultiplexer_47_out0), .out1(demultiplexer_47_out1), .in(demultiplexer_23_out1), .sel(P));  // open: en
  Demultiplexer demultiplexer_48 (
    .out0(demultiplexer_48_out0), .out1(demultiplexer_48_out1), .in(demultiplexer_24_out0), .sel(P));  // open: en
  Demultiplexer demultiplexer_49 (
    .out0(demultiplexer_49_out0), .out1(demultiplexer_49_out1), .in(demultiplexer_24_out1), .sel(P));  // open: en
  Demultiplexer demultiplexer_50 (
    .out0(demultiplexer_50_out0), .out1(demultiplexer_50_out1), .in(demultiplexer_25_out0), .sel(P));  // open: en
  Demultiplexer demultiplexer_51 (
    .out0(demultiplexer_51_out0), .out1(demultiplexer_51_out1), .in(demultiplexer_25_out1), .sel(P));  // open: en
  Demultiplexer demultiplexer_52 (
    .out0(demultiplexer_52_out0), .out1(demultiplexer_52_out1), .in(demultiplexer_26_out0), .sel(P));  // open: en
  Demultiplexer demultiplexer_53 (
    .out0(demultiplexer_53_out0), .out1(demultiplexer_53_out1), .in(demultiplexer_26_out1), .sel(P));  // open: en
  Demultiplexer demultiplexer_54 (
    .out0(demultiplexer_54_out0), .out1(demultiplexer_54_out1), .in(demultiplexer_27_out0), .sel(P));  // open: en
  Demultiplexer demultiplexer_55 (
    .out0(demultiplexer_55_out0), .out1(demultiplexer_55_out1), .in(demultiplexer_27_out1), .sel(P));  // open: en
  Demultiplexer demultiplexer_56 (
    .out0(demultiplexer_56_out0), .out1(demultiplexer_56_out1), .in(demultiplexer_28_out0), .sel(P));  // open: en
  Demultiplexer demultiplexer_57 (
    .out0(demultiplexer_57_out0), .out1(demultiplexer_57_out1), .in(demultiplexer_28_out1), .sel(P));  // open: en
  Demultiplexer demultiplexer_58 (
    .out0(demultiplexer_58_out0), .out1(demultiplexer_58_out1), .in(demultiplexer_29_out0), .sel(P));  // open: en
  Demultiplexer demultiplexer_59 (
    .out0(demultiplexer_59_out0), .out1(demultiplexer_59_out1), .in(demultiplexer_29_out1), .sel(P));  // open: en
  Demultiplexer demultiplexer_60 (
    .out0(demultiplexer_60_out0), .out1(demultiplexer_60_out1), .in(demultiplexer_30_out0), .sel(P));  // open: en
  Demultiplexer demultiplexer_61 (
    .out0(demultiplexer_61_out0), .out1(demultiplexer_61_out1), .in(demultiplexer_30_out1), .sel(P));  // open: en
  Demultiplexer demultiplexer_62 (
    .out0(demultiplexer_62_out0), .out1(demultiplexer_62_out1), .in(demultiplexer_31_out0), .sel(P));  // open: en
  Demultiplexer demultiplexer_63 (
    .out0(demultiplexer_63_out0), .out1(demultiplexer_63_out1), .in(demultiplexer_31_out1), .sel(P));  // open: en
  S_R_Flip_Flop #(.trigger("falling")) s_r_ff_1 (
    .S(demultiplexer_32_out1), .clk(CLK), .R(demultiplexer_32_out0), .Q(MEM[31]));  // open: Qn, preset, reset, en
  S_R_Flip_Flop #(.trigger("falling")) s_r_ff_2 (
    .S(demultiplexer_33_out1), .clk(CLK), .R(demultiplexer_33_out0), .Q(MEM[30]));  // open: Qn, preset, reset, en
  S_R_Flip_Flop #(.trigger("falling")) s_r_ff_3 (
    .S(demultiplexer_34_out1), .clk(CLK), .R(demultiplexer_34_out0), .Q(MEM[29]));  // open: Qn, preset, reset, en
  S_R_Flip_Flop #(.trigger("falling")) s_r_ff_4 (
    .S(demultiplexer_35_out1), .clk(CLK), .R(demultiplexer_35_out0), .Q(MEM[28]));  // open: Qn, preset, reset, en
  S_R_Flip_Flop #(.trigger("falling")) s_r_ff_5 (
    .S(demultiplexer_36_out1), .clk(CLK), .R(demultiplexer_36_out0), .Q(MEM[27]));  // open: Qn, preset, reset, en
  S_R_Flip_Flop #(.trigger("falling")) s_r_ff_6 (
    .S(demultiplexer_37_out1), .clk(CLK), .R(demultiplexer_37_out0), .Q(MEM[26]));  // open: Qn, preset, reset, en
  S_R_Flip_Flop #(.trigger("falling")) s_r_ff_7 (
    .S(demultiplexer_38_out1), .clk(CLK), .R(demultiplexer_38_out0), .Q(MEM[25]));  // open: Qn, preset, reset, en
  S_R_Flip_Flop #(.trigger("falling")) s_r_ff_8 (
    .S(demultiplexer_39_out1), .clk(CLK), .R(demultiplexer_39_out0), .Q(MEM[24]));  // open: Qn, preset, reset, en
  S_R_Flip_Flop #(.trigger("falling")) s_r_ff_9 (
    .S(demultiplexer_40_out1), .clk(CLK), .R(demultiplexer_40_out0), .Q(MEM[23]));  // open: Qn, preset, reset, en
  S_R_Flip_Flop #(.trigger("falling")) s_r_ff_10 (
    .S(demultiplexer_41_out1), .clk(CLK), .R(demultiplexer_41_out0), .Q(MEM[22]));  // open: Qn, preset, reset, en
  S_R_Flip_Flop #(.trigger("falling")) s_r_ff_11 (
    .S(demultiplexer_42_out1), .clk(CLK), .R(demultiplexer_42_out0), .Q(MEM[21]));  // open: Qn, preset, reset, en
  S_R_Flip_Flop #(.trigger("falling")) s_r_ff_12 (
    .S(demultiplexer_43_out1), .clk(CLK), .R(demultiplexer_43_out0), .Q(MEM[20]));  // open: Qn, preset, reset, en
  S_R_Flip_Flop #(.trigger("falling")) s_r_ff_13 (
    .S(demultiplexer_44_out1), .clk(CLK), .R(demultiplexer_44_out0), .Q(MEM[19]));  // open: Qn, preset, reset, en
  S_R_Flip_Flop #(.trigger("falling")) s_r_ff_14 (
    .S(demultiplexer_45_out1), .clk(CLK), .R(demultiplexer_45_out0), .Q(MEM[18]));  // open: Qn, preset, reset, en
  S_R_Flip_Flop #(.trigger("falling")) s_r_ff_15 (
    .S(demultiplexer_46_out1), .clk(CLK), .R(demultiplexer_46_out0), .Q(MEM[17]));  // open: Qn, preset, reset, en
  S_R_Flip_Flop #(.trigger("falling")) s_r_ff_16 (
    .S(demultiplexer_47_out1), .clk(CLK), .R(demultiplexer_47_out0), .Q(MEM[16]));  // open: Qn, preset, reset, en
  S_R_Flip_Flop #(.trigger("falling")) s_r_ff_17 (
    .S(demultiplexer_48_out1), .clk(CLK), .R(demultiplexer_48_out0), .Q(MEM[15]));  // open: Qn, preset, reset, en
  S_R_Flip_Flop #(.trigger("falling")) s_r_ff_18 (
    .S(demultiplexer_49_out1), .clk(CLK), .R(demultiplexer_49_out0), .Q(MEM[14]));  // open: Qn, preset, reset, en
  S_R_Flip_Flop #(.trigger("falling")) s_r_ff_19 (
    .S(demultiplexer_50_out1), .clk(CLK), .R(demultiplexer_50_out0), .Q(MEM[13]));  // open: Qn, preset, reset, en
  S_R_Flip_Flop #(.trigger("falling")) s_r_ff_20 (
    .S(demultiplexer_51_out1), .clk(CLK), .R(demultiplexer_51_out0), .Q(MEM[12]));  // open: Qn, preset, reset, en
  S_R_Flip_Flop #(.trigger("falling")) s_r_ff_21 (
    .S(demultiplexer_52_out1), .clk(CLK), .R(demultiplexer_52_out0), .Q(MEM[11]));  // open: Qn, preset, reset, en
  S_R_Flip_Flop #(.trigger("falling")) s_r_ff_22 (
    .S(demultiplexer_53_out1), .clk(CLK), .R(demultiplexer_53_out0), .Q(MEM[10]));  // open: Qn, preset, reset, en
  S_R_Flip_Flop #(.trigger("falling")) s_r_ff_23 (
    .S(demultiplexer_54_out1), .clk(CLK), .R(demultiplexer_54_out0), .Q(MEM[9]));  // open: Qn, preset, reset, en
  S_R_Flip_Flop #(.trigger("falling")) s_r_ff_24 (
    .S(demultiplexer_55_out1), .clk(CLK), .R(demultiplexer_55_out0), .Q(MEM[8]));  // open: Qn, preset, reset, en
  S_R_Flip_Flop #(.trigger("falling")) s_r_ff_25 (
    .S(demultiplexer_56_out1), .clk(CLK), .R(demultiplexer_56_out0), .Q(MEM[7]));  // open: Qn, preset, reset, en
  S_R_Flip_Flop #(.trigger("falling")) s_r_ff_26 (
    .S(demultiplexer_57_out1), .clk(CLK), .R(demultiplexer_57_out0), .Q(MEM[6]));  // open: Qn, preset, reset, en
  S_R_Flip_Flop #(.trigger("falling")) s_r_ff_27 (
    .S(demultiplexer_58_out1), .clk(CLK), .R(demultiplexer_58_out0), .Q(MEM[5]));  // open: Qn, preset, reset, en
  S_R_Flip_Flop #(.trigger("falling")) s_r_ff_28 (
    .S(demultiplexer_59_out1), .clk(CLK), .R(demultiplexer_59_out0), .Q(MEM[4]));  // open: Qn, preset, reset, en
  S_R_Flip_Flop #(.trigger("falling")) s_r_ff_29 (
    .S(demultiplexer_60_out1), .clk(CLK), .R(demultiplexer_60_out0), .Q(MEM[3]));  // open: Qn, preset, reset, en
  S_R_Flip_Flop #(.trigger("falling")) s_r_ff_30 (
    .S(demultiplexer_61_out1), .clk(CLK), .R(demultiplexer_61_out0), .Q(MEM[2]));  // open: Qn, preset, reset, en
  S_R_Flip_Flop #(.trigger("falling")) s_r_ff_31 (
    .S(demultiplexer_62_out1), .clk(CLK), .R(demultiplexer_62_out0), .Q(MEM[1]));  // open: Qn, preset, reset, en
  S_R_Flip_Flop #(.trigger("falling")) s_r_ff_32 (
    .S(demultiplexer_63_out1), .clk(CLK), .R(demultiplexer_63_out0), .Q(MEM[0]));  // open: Qn, preset, reset, en
endmodule

module MM10 (
  input  [4:0] X,
  input  CLK,
  input  SEL,
  input  [4:0] Y,
  input  P,
  output [31:0] R00,
  output [31:0] R01,
  output [31:0] R02,
  output [31:0] R03,
  output [31:0] R04,
  output [31:0] R05,
  output [31:0] R06,
  output [31:0] R07,
  output [31:0] R08,
  output [31:0] R09,
  output [31:0] R0A,
  output [31:0] R0B,
  output [31:0] R0C,
  output [31:0] R0D,
  output [31:0] R0E,
  output [31:0] R0F,
  output [31:0] R10,
  output [31:0] R11,
  output [31:0] R12,
  output [31:0] R13,
  output [31:0] R14,
  output [31:0] R15,
  output [31:0] R16,
  output [31:0] R17,
  output [31:0] R18,
  output [31:0] R19,
  output [31:0] R1A,
  output [31:0] R1B,
  output [31:0] R1C,
  output [31:0] R1D,
  output [31:0] R1E,
  output [31:0] R1F
);

  wire demultiplexer_1_out0, demultiplexer_1_out1, demultiplexer_2_out0, demultiplexer_2_out1,
       demultiplexer_3_out0, demultiplexer_3_out1, demultiplexer_4_out0, demultiplexer_4_out1,
       demultiplexer_5_out0, demultiplexer_5_out1, demultiplexer_6_out0, demultiplexer_6_out1,
       demultiplexer_7_out0, demultiplexer_7_out1, demultiplexer_8_out0, demultiplexer_8_out1,
       demultiplexer_9_out0, demultiplexer_9_out1, demultiplexer_10_out0, demultiplexer_10_out1,
       demultiplexer_11_out0, demultiplexer_11_out1, demultiplexer_12_out0, demultiplexer_12_out1,
       demultiplexer_13_out0, demultiplexer_13_out1, demultiplexer_14_out0, demultiplexer_14_out1,
       demultiplexer_15_out0, demultiplexer_15_out1, demultiplexer_16_out0, demultiplexer_16_out1,
       demultiplexer_17_out0, demultiplexer_17_out1, demultiplexer_18_out0, demultiplexer_18_out1,
       demultiplexer_19_out0, demultiplexer_19_out1, demultiplexer_20_out0, demultiplexer_20_out1,
       demultiplexer_21_out0, demultiplexer_21_out1, demultiplexer_22_out0, demultiplexer_22_out1,
       demultiplexer_23_out0, demultiplexer_23_out1, demultiplexer_24_out0, demultiplexer_24_out1,
       demultiplexer_25_out0, demultiplexer_25_out1, demultiplexer_26_out0, demultiplexer_26_out1,
       demultiplexer_27_out0, demultiplexer_27_out1, demultiplexer_28_out0, demultiplexer_28_out1,
       demultiplexer_29_out0, demultiplexer_29_out1, demultiplexer_30_out0, demultiplexer_30_out1,
       demultiplexer_31_out0, demultiplexer_31_out1;

  Demultiplexer demultiplexer_1 (
    .out0(demultiplexer_1_out0), .out1(demultiplexer_1_out1), .in(SEL), .sel(Y[4]));  // open: en
  Demultiplexer demultiplexer_2 (
    .out0(demultiplexer_2_out0), .out1(demultiplexer_2_out1), .in(demultiplexer_1_out0), .sel(Y[3]));  // open: en
  Demultiplexer demultiplexer_3 (
    .out0(demultiplexer_3_out0), .out1(demultiplexer_3_out1), .in(demultiplexer_1_out1), .sel(Y[3]));  // open: en
  Demultiplexer demultiplexer_4 (
    .out0(demultiplexer_4_out0), .out1(demultiplexer_4_out1), .in(demultiplexer_2_out0), .sel(Y[2]));  // open: en
  Demultiplexer demultiplexer_5 (
    .out0(demultiplexer_5_out0), .out1(demultiplexer_5_out1), .in(demultiplexer_2_out1), .sel(Y[2]));  // open: en
  Demultiplexer demultiplexer_6 (
    .out0(demultiplexer_6_out0), .out1(demultiplexer_6_out1), .in(demultiplexer_3_out0), .sel(Y[2]));  // open: en
  Demultiplexer demultiplexer_7 (
    .out0(demultiplexer_7_out0), .out1(demultiplexer_7_out1), .in(demultiplexer_3_out1), .sel(Y[2]));  // open: en
  Demultiplexer demultiplexer_8 (
    .out0(demultiplexer_8_out0), .out1(demultiplexer_8_out1), .in(demultiplexer_4_out0), .sel(Y[1]));  // open: en
  Demultiplexer demultiplexer_9 (
    .out0(demultiplexer_9_out0), .out1(demultiplexer_9_out1), .in(demultiplexer_4_out1), .sel(Y[1]));  // open: en
  Demultiplexer demultiplexer_10 (
    .out0(demultiplexer_10_out0), .out1(demultiplexer_10_out1), .in(demultiplexer_5_out0), .sel(Y[1]));  // open: en
  Demultiplexer demultiplexer_11 (
    .out0(demultiplexer_11_out0), .out1(demultiplexer_11_out1), .in(demultiplexer_5_out1), .sel(Y[1]));  // open: en
  Demultiplexer demultiplexer_12 (
    .out0(demultiplexer_12_out0), .out1(demultiplexer_12_out1), .in(demultiplexer_6_out0), .sel(Y[1]));  // open: en
  Demultiplexer demultiplexer_13 (
    .out0(demultiplexer_13_out0), .out1(demultiplexer_13_out1), .in(demultiplexer_6_out1), .sel(Y[1]));  // open: en
  Demultiplexer demultiplexer_14 (
    .out0(demultiplexer_14_out0), .out1(demultiplexer_14_out1), .in(demultiplexer_7_out0), .sel(Y[1]));  // open: en
  Demultiplexer demultiplexer_15 (
    .out0(demultiplexer_15_out0), .out1(demultiplexer_15_out1), .in(demultiplexer_7_out1), .sel(Y[1]));  // open: en
  Demultiplexer demultiplexer_16 (
    .out0(demultiplexer_16_out0), .out1(demultiplexer_16_out1), .in(demultiplexer_8_out0), .sel(Y[0]));  // open: en
  Demultiplexer demultiplexer_17 (
    .out0(demultiplexer_17_out0), .out1(demultiplexer_17_out1), .in(demultiplexer_8_out1), .sel(Y[0]));  // open: en
  Demultiplexer demultiplexer_18 (
    .out0(demultiplexer_18_out0), .out1(demultiplexer_18_out1), .in(demultiplexer_9_out0), .sel(Y[0]));  // open: en
  Demultiplexer demultiplexer_19 (
    .out0(demultiplexer_19_out0), .out1(demultiplexer_19_out1), .in(demultiplexer_9_out1), .sel(Y[0]));  // open: en
  Demultiplexer demultiplexer_20 (
    .out0(demultiplexer_20_out0), .out1(demultiplexer_20_out1), .in(demultiplexer_10_out0), .sel(Y[0]));  // open: en
  Demultiplexer demultiplexer_21 (
    .out0(demultiplexer_21_out0), .out1(demultiplexer_21_out1), .in(demultiplexer_10_out1), .sel(Y[0]));  // open: en
  Demultiplexer demultiplexer_22 (
    .out0(demultiplexer_22_out0), .out1(demultiplexer_22_out1), .in(demultiplexer_11_out0), .sel(Y[0]));  // open: en
  Demultiplexer demultiplexer_23 (
    .out0(demultiplexer_23_out0), .out1(demultiplexer_23_out1), .in(demultiplexer_11_out1), .sel(Y[0]));  // open: en
  Demultiplexer demultiplexer_24 (
    .out0(demultiplexer_24_out0), .out1(demultiplexer_24_out1), .in(demultiplexer_12_out0), .sel(Y[0]));  // open: en
  Demultiplexer demultiplexer_25 (
    .out0(demultiplexer_25_out0), .out1(demultiplexer_25_out1), .in(demultiplexer_12_out1), .sel(Y[0]));  // open: en
  Demultiplexer demultiplexer_26 (
    .out0(demultiplexer_26_out0), .out1(demultiplexer_26_out1), .in(demultiplexer_13_out0), .sel(Y[0]));  // open: en
  Demultiplexer demultiplexer_27 (
    .out0(demultiplexer_27_out0), .out1(demultiplexer_27_out1), .in(demultiplexer_13_out1), .sel(Y[0]));  // open: en
  Demultiplexer demultiplexer_28 (
    .out0(demultiplexer_28_out0), .out1(demultiplexer_28_out1), .in(demultiplexer_14_out0), .sel(Y[0]));  // open: en
  Demultiplexer demultiplexer_29 (
    .out0(demultiplexer_29_out0), .out1(demultiplexer_29_out1), .in(demultiplexer_14_out1), .sel(Y[0]));  // open: en
  Demultiplexer demultiplexer_30 (
    .out0(demultiplexer_30_out0), .out1(demultiplexer_30_out1), .in(demultiplexer_15_out0), .sel(Y[0]));  // open: en
  Demultiplexer demultiplexer_31 (
    .out0(demultiplexer_31_out0), .out1(demultiplexer_31_out1), .in(demultiplexer_15_out1), .sel(Y[0]));  // open: en
  MemRow5 memrow5_1 (
    .SEL(demultiplexer_16_out0), .ADR_1(X[3]), .ADR_2(X[2]), .ADR_3(X[1]), .ADR_4(X[0]), .P(P), .CLK(CLK),
    .ADR_0(X[4]), .MEM(R00));
  MemRow5 memrow5_2 (
    .SEL(demultiplexer_16_out1), .ADR_1(X[3]), .ADR_2(X[2]), .ADR_3(X[1]), .ADR_4(X[0]), .P(P), .CLK(CLK),
    .ADR_0(X[4]), .MEM(R01));
  MemRow5 memrow5_3 (
    .SEL(demultiplexer_17_out0), .ADR_1(X[3]), .ADR_2(X[2]), .ADR_3(X[1]), .ADR_4(X[0]), .P(P), .CLK(CLK),
    .ADR_0(X[4]), .MEM(R02));
  MemRow5 memrow5_4 (
    .SEL(demultiplexer_17_out1), .ADR_1(X[3]), .ADR_2(X[2]), .ADR_3(X[1]), .ADR_4(X[0]), .P(P), .CLK(CLK),
    .ADR_0(X[4]), .MEM(R03));
  MemRow5 memrow5_5 (
    .SEL(demultiplexer_18_out0), .ADR_1(X[3]), .ADR_2(X[2]), .ADR_3(X[1]), .ADR_4(X[0]), .P(P), .CLK(CLK),
    .ADR_0(X[4]), .MEM(R04));
  MemRow5 memrow5_6 (
    .SEL(demultiplexer_18_out1), .ADR_1(X[3]), .ADR_2(X[2]), .ADR_3(X[1]), .ADR_4(X[0]), .P(P), .CLK(CLK),
    .ADR_0(X[4]), .MEM(R05));
  MemRow5 memrow5_7 (
    .SEL(demultiplexer_19_out0), .ADR_1(X[3]), .ADR_2(X[2]), .ADR_3(X[1]), .ADR_4(X[0]), .P(P), .CLK(CLK),
    .ADR_0(X[4]), .MEM(R06));
  MemRow5 memrow5_8 (
    .SEL(demultiplexer_19_out1), .ADR_1(X[3]), .ADR_2(X[2]), .ADR_3(X[1]), .ADR_4(X[0]), .P(P), .CLK(CLK),
    .ADR_0(X[4]), .MEM(R07));
  MemRow5 memrow5_9 (
    .SEL(demultiplexer_20_out0), .ADR_1(X[3]), .ADR_2(X[2]), .ADR_3(X[1]), .ADR_4(X[0]), .P(P), .CLK(CLK),
    .ADR_0(X[4]), .MEM(R08));
  MemRow5 memrow5_10 (
    .SEL(demultiplexer_20_out1), .ADR_1(X[3]), .ADR_2(X[2]), .ADR_3(X[1]), .ADR_4(X[0]), .P(P), .CLK(CLK),
    .ADR_0(X[4]), .MEM(R09));
  MemRow5 memrow5_11 (
    .SEL(demultiplexer_21_out0), .ADR_1(X[3]), .ADR_2(X[2]), .ADR_3(X[1]), .ADR_4(X[0]), .P(P), .CLK(CLK),
    .ADR_0(X[4]), .MEM(R0A));
  MemRow5 memrow5_12 (
    .SEL(demultiplexer_21_out1), .ADR_1(X[3]), .ADR_2(X[2]), .ADR_3(X[1]), .ADR_4(X[0]), .P(P), .CLK(CLK),
    .ADR_0(X[4]), .MEM(R0B));
  MemRow5 memrow5_13 (
    .SEL(demultiplexer_22_out0), .ADR_1(X[3]), .ADR_2(X[2]), .ADR_3(X[1]), .ADR_4(X[0]), .P(P), .CLK(CLK),
    .ADR_0(X[4]), .MEM(R0C));
  MemRow5 memrow5_14 (
    .SEL(demultiplexer_22_out1), .ADR_1(X[3]), .ADR_2(X[2]), .ADR_3(X[1]), .ADR_4(X[0]), .P(P), .CLK(CLK),
    .ADR_0(X[4]), .MEM(R0D));
  MemRow5 memrow5_15 (
    .SEL(demultiplexer_23_out0), .ADR_1(X[3]), .ADR_2(X[2]), .ADR_3(X[1]), .ADR_4(X[0]), .P(P), .CLK(CLK),
    .ADR_0(X[4]), .MEM(R0E));
  MemRow5 memrow5_16 (
    .SEL(demultiplexer_23_out1), .ADR_1(X[3]), .ADR_2(X[2]), .ADR_3(X[1]), .ADR_4(X[0]), .P(P), .CLK(CLK),
    .ADR_0(X[4]), .MEM(R0F));
  MemRow5 memrow5_17 (
    .SEL(demultiplexer_24_out0), .ADR_1(X[3]), .ADR_2(X[2]), .ADR_3(X[1]), .ADR_4(X[0]), .P(P), .CLK(CLK),
    .ADR_0(X[4]), .MEM(R10));
  MemRow5 memrow5_18 (
    .SEL(demultiplexer_24_out1), .ADR_1(X[3]), .ADR_2(X[2]), .ADR_3(X[1]), .ADR_4(X[0]), .P(P), .CLK(CLK),
    .ADR_0(X[4]), .MEM(R11));
  MemRow5 memrow5_19 (
    .SEL(demultiplexer_25_out0), .ADR_1(X[3]), .ADR_2(X[2]), .ADR_3(X[1]), .ADR_4(X[0]), .P(P), .CLK(CLK),
    .ADR_0(X[4]), .MEM(R12));
  MemRow5 memrow5_20 (
    .SEL(demultiplexer_25_out1), .ADR_1(X[3]), .ADR_2(X[2]), .ADR_3(X[1]), .ADR_4(X[0]), .P(P), .CLK(CLK),
    .ADR_0(X[4]), .MEM(R13));
  MemRow5 memrow5_21 (
    .SEL(demultiplexer_26_out0), .ADR_1(X[3]), .ADR_2(X[2]), .ADR_3(X[1]), .ADR_4(X[0]), .P(P), .CLK(CLK),
    .ADR_0(X[4]), .MEM(R14));
  MemRow5 memrow5_22 (
    .SEL(demultiplexer_26_out1), .ADR_1(X[3]), .ADR_2(X[2]), .ADR_3(X[1]), .ADR_4(X[0]), .P(P), .CLK(CLK),
    .ADR_0(X[4]), .MEM(R15));
  MemRow5 memrow5_23 (
    .SEL(demultiplexer_27_out0), .ADR_1(X[3]), .ADR_2(X[2]), .ADR_3(X[1]), .ADR_4(X[0]), .P(P), .CLK(CLK),
    .ADR_0(X[4]), .MEM(R16));
  MemRow5 memrow5_24 (
    .SEL(demultiplexer_27_out1), .ADR_1(X[3]), .ADR_2(X[2]), .ADR_3(X[1]), .ADR_4(X[0]), .P(P), .CLK(CLK),
    .ADR_0(X[4]), .MEM(R17));
  MemRow5 memrow5_25 (
    .SEL(demultiplexer_28_out0), .ADR_1(X[3]), .ADR_2(X[2]), .ADR_3(X[1]), .ADR_4(X[0]), .P(P), .CLK(CLK),
    .ADR_0(X[4]), .MEM(R18));
  MemRow5 memrow5_26 (
    .SEL(demultiplexer_28_out1), .ADR_1(X[3]), .ADR_2(X[2]), .ADR_3(X[1]), .ADR_4(X[0]), .P(P), .CLK(CLK),
    .ADR_0(X[4]), .MEM(R19));
  MemRow5 memrow5_27 (
    .SEL(demultiplexer_29_out0), .ADR_1(X[3]), .ADR_2(X[2]), .ADR_3(X[1]), .ADR_4(X[0]), .P(P), .CLK(CLK),
    .ADR_0(X[4]), .MEM(R1A));
  MemRow5 memrow5_28 (
    .SEL(demultiplexer_29_out1), .ADR_1(X[3]), .ADR_2(X[2]), .ADR_3(X[1]), .ADR_4(X[0]), .P(P), .CLK(CLK),
    .ADR_0(X[4]), .MEM(R1B));
  MemRow5 memrow5_29 (
    .SEL(demultiplexer_30_out0), .ADR_1(X[3]), .ADR_2(X[2]), .ADR_3(X[1]), .ADR_4(X[0]), .P(P), .CLK(CLK),
    .ADR_0(X[4]), .MEM(R1C));
  MemRow5 memrow5_30 (
    .SEL(demultiplexer_30_out1), .ADR_1(X[3]), .ADR_2(X[2]), .ADR_3(X[1]), .ADR_4(X[0]), .P(P), .CLK(CLK),
    .ADR_0(X[4]), .MEM(R1D));
  MemRow5 memrow5_31 (
    .SEL(demultiplexer_31_out0), .ADR_1(X[3]), .ADR_2(X[2]), .ADR_3(X[1]), .ADR_4(X[0]), .P(P), .CLK(CLK),
    .ADR_0(X[4]), .MEM(R1E));
  MemRow5 memrow5_32 (
    .SEL(demultiplexer_31_out1), .ADR_1(X[3]), .ADR_2(X[2]), .ADR_3(X[1]), .ADR_4(X[0]), .P(P), .CLK(CLK),
    .ADR_0(X[4]), .MEM(R1F));
endmodule

module Cell1 (
  input  CLK,
  input  W,
  input  [4:0] IN,
  input  R,
  input  R2,
  output [4:0] OUT,
  output [4:0] OUT2
);

  wire demultiplexer_1_out0, demultiplexer_1_out1, demultiplexer_2_out0, demultiplexer_2_out1,
       demultiplexer_3_out0, demultiplexer_3_out1, demultiplexer_4_out0, demultiplexer_4_out1,
       demultiplexer_5_out0, demultiplexer_5_out1, s_r_ff_1_q, s_r_ff_2_q, s_r_ff_3_q, s_r_ff_4_q, s_r_ff_5_q;

  Demultiplexer demultiplexer_1 (
    .out0(demultiplexer_1_out0), .out1(demultiplexer_1_out1), .in(W), .sel(IN[0]));  // open: en
  Demultiplexer demultiplexer_2 (
    .out0(demultiplexer_2_out0), .out1(demultiplexer_2_out1), .in(W), .sel(IN[1]));  // open: en
  Demultiplexer demultiplexer_3 (
    .out0(demultiplexer_3_out0), .out1(demultiplexer_3_out1), .in(W), .sel(IN[2]));  // open: en
  Demultiplexer demultiplexer_4 (
    .out0(demultiplexer_4_out0), .out1(demultiplexer_4_out1), .in(W), .sel(IN[3]));  // open: en
  Demultiplexer demultiplexer_5 (
    .out0(demultiplexer_5_out0), .out1(demultiplexer_5_out1), .in(W), .sel(IN[4]));  // open: en
  S_R_Flip_Flop #(.trigger("falling")) s_r_ff_1 (
    .S(demultiplexer_1_out1), .clk(CLK), .R(demultiplexer_1_out0), .Q(s_r_ff_1_q));  // open: Qn, preset, reset, en
  S_R_Flip_Flop #(.trigger("falling")) s_r_ff_2 (
    .S(demultiplexer_2_out1), .clk(CLK), .R(demultiplexer_2_out0), .Q(s_r_ff_2_q));  // open: Qn, preset, reset, en
  S_R_Flip_Flop #(.trigger("falling")) s_r_ff_3 (
    .S(demultiplexer_3_out1), .clk(CLK), .R(demultiplexer_3_out0), .Q(s_r_ff_3_q));  // open: Qn, preset, reset, en
  S_R_Flip_Flop #(.trigger("falling")) s_r_ff_4 (
    .S(demultiplexer_4_out1), .clk(CLK), .R(demultiplexer_4_out0), .Q(s_r_ff_4_q));  // open: Qn, preset, reset, en
  S_R_Flip_Flop #(.trigger("falling")) s_r_ff_5 (
    .S(demultiplexer_5_out1), .clk(CLK), .R(demultiplexer_5_out0), .Q(s_r_ff_5_q));  // open: Qn, preset, reset, en
  and and_1 (OUT[0], R, s_r_ff_1_q);
  and and_2 (OUT[1], R, s_r_ff_2_q);
  and and_3 (OUT[2], R, s_r_ff_3_q);
  and and_4 (OUT[3], R, s_r_ff_4_q);
  and and_5 (OUT[4], R, s_r_ff_5_q);
  and and_6 (OUT2[0], R2, s_r_ff_1_q);
  and and_7 (OUT2[1], R2, s_r_ff_2_q);
  and and_8 (OUT2[2], R2, s_r_ff_3_q);
  and and_9 (OUT2[3], R2, s_r_ff_4_q);
  and and_10 (OUT2[4], R2, s_r_ff_5_q);
endmodule

module RAM5 (
  input  R,
  input  W,
  input  [4:0] IN,
  input  CLK,
  input  SEL,
  input  [4:0] ADR,
  input  [4:0] ADR2,
  input  R2,
  output [4:0] OUT,
  output [4:0] OUT2
);

  wire and_1_out, and_2_out, and_3_out, and_4_out, and_5_out, and_6_out, and_7_out, and_8_out, and_9_out,
       and_10_out, and_11_out, and_12_out, and_13_out, and_14_out, and_15_out, and_16_out, and_17_out,
       and_18_out, and_19_out, and_20_out, and_21_out, and_22_out, and_23_out, and_24_out, and_25_out,
       and_26_out, and_27_out, and_28_out, and_29_out, and_30_out, and_31_out, and_32_out, and_33_out,
       and_34_out, and_35_out, and_36_out, and_37_out, and_38_out, and_39_out, and_40_out, and_41_out,
       and_42_out, and_43_out, and_44_out, and_45_out, and_46_out, and_47_out, and_48_out, and_49_out,
       and_50_out, and_51_out, and_52_out, and_53_out, and_54_out, and_55_out, and_56_out, and_57_out,
       and_58_out, and_59_out, and_60_out, and_61_out, and_62_out, and_63_out, and_64_out,
       demultiplexer_1_out0, demultiplexer_1_out1, demultiplexer_1_out2, demultiplexer_1_out3,
       demultiplexer_1_out4, demultiplexer_1_out5, demultiplexer_1_out6, demultiplexer_1_out7,
       demultiplexer_1_out8, demultiplexer_1_out9, demultiplexer_1_out10, demultiplexer_1_out11,
       demultiplexer_1_out12, demultiplexer_1_out13, demultiplexer_1_out14, demultiplexer_1_out15,
       demultiplexer_1_out16, demultiplexer_1_out17, demultiplexer_1_out18, demultiplexer_1_out19,
       demultiplexer_1_out20, demultiplexer_1_out21, demultiplexer_1_out22, demultiplexer_1_out23,
       demultiplexer_1_out24, demultiplexer_1_out25, demultiplexer_1_out26, demultiplexer_1_out27,
       demultiplexer_1_out28, demultiplexer_1_out29, demultiplexer_1_out30, demultiplexer_1_out31,
       demultiplexer_2_out0, demultiplexer_2_out1, demultiplexer_2_out2, demultiplexer_2_out3,
       demultiplexer_2_out4, demultiplexer_2_out5, demultiplexer_2_out6, demultiplexer_2_out7,
       demultiplexer_2_out8, demultiplexer_2_out9, demultiplexer_2_out10, demultiplexer_2_out11,
       demultiplexer_2_out12, demultiplexer_2_out13, demultiplexer_2_out14, demultiplexer_2_out15,
       demultiplexer_2_out16, demultiplexer_2_out17, demultiplexer_2_out18, demultiplexer_2_out19,
       demultiplexer_2_out20, demultiplexer_2_out21, demultiplexer_2_out22, demultiplexer_2_out23,
       demultiplexer_2_out24, demultiplexer_2_out25, demultiplexer_2_out26, demultiplexer_2_out27,
       demultiplexer_2_out28, demultiplexer_2_out29, demultiplexer_2_out30, demultiplexer_2_out31;
  wire [4:0] cell1_1_out, cell1_1_out2, cell1_2_out, cell1_2_out2, cell1_3_out, cell1_3_out2, cell1_4_out,
       cell1_4_out2, cell1_5_out, cell1_5_out2, cell1_6_out, cell1_6_out2, cell1_7_out, cell1_7_out2,
       cell1_8_out, cell1_8_out2, cell1_9_out, cell1_9_out2, cell1_10_out, cell1_10_out2, cell1_11_out,
       cell1_11_out2, cell1_12_out, cell1_12_out2, cell1_13_out, cell1_13_out2, cell1_14_out, cell1_14_out2,
       cell1_15_out, cell1_15_out2, cell1_16_out, cell1_16_out2, cell1_17_out, cell1_17_out2, cell1_18_out,
       cell1_18_out2, cell1_19_out, cell1_19_out2, cell1_20_out, cell1_20_out2, cell1_21_out, cell1_21_out2,
       cell1_22_out, cell1_22_out2, cell1_23_out, cell1_23_out2, cell1_24_out, cell1_24_out2, cell1_25_out,
       cell1_25_out2, cell1_26_out, cell1_26_out2, cell1_27_out, cell1_27_out2, cell1_28_out, cell1_28_out2,
       cell1_29_out, cell1_29_out2, cell1_30_out, cell1_30_out2, cell1_31_out, cell1_31_out2, cell1_32_out,
       cell1_32_out2;

  Demultiplexer #(.select(5)) demultiplexer_1 (
    .out0(demultiplexer_1_out0), .out1(demultiplexer_1_out1), .out2(demultiplexer_1_out2),
    .out3(demultiplexer_1_out3), .out4(demultiplexer_1_out4), .out5(demultiplexer_1_out5),
    .out6(demultiplexer_1_out6), .out7(demultiplexer_1_out7), .out8(demultiplexer_1_out8),
    .out9(demultiplexer_1_out9), .out10(demultiplexer_1_out10), .out11(demultiplexer_1_out11),
    .out12(demultiplexer_1_out12), .out13(demultiplexer_1_out13), .out14(demultiplexer_1_out14),
    .out15(demultiplexer_1_out15), .out16(demultiplexer_1_out16), .out17(demultiplexer_1_out17),
    .out18(demultiplexer_1_out18), .out19(demultiplexer_1_out19), .out20(demultiplexer_1_out20),
    .out21(demultiplexer_1_out21), .out22(demultiplexer_1_out22), .out23(demultiplexer_1_out23),
    .out24(demultiplexer_1_out24), .out25(demultiplexer_1_out25), .out26(demultiplexer_1_out26),
    .out27(demultiplexer_1_out27), .out28(demultiplexer_1_out28), .out29(demultiplexer_1_out29),
    .out30(demultiplexer_1_out30), .out31(demultiplexer_1_out31), .in(SEL), .sel(ADR));  // open: en
  Demultiplexer #(.select(5)) demultiplexer_2 (
    .out0(demultiplexer_2_out0), .out1(demultiplexer_2_out1), .out2(demultiplexer_2_out2),
    .out3(demultiplexer_2_out3), .out4(demultiplexer_2_out4), .out5(demultiplexer_2_out5),
    .out6(demultiplexer_2_out6), .out7(demultiplexer_2_out7), .out8(demultiplexer_2_out8),
    .out9(demultiplexer_2_out9), .out10(demultiplexer_2_out10), .out11(demultiplexer_2_out11),
    .out12(demultiplexer_2_out12), .out13(demultiplexer_2_out13), .out14(demultiplexer_2_out14),
    .out15(demultiplexer_2_out15), .out16(demultiplexer_2_out16), .out17(demultiplexer_2_out17),
    .out18(demultiplexer_2_out18), .out19(demultiplexer_2_out19), .out20(demultiplexer_2_out20),
    .out21(demultiplexer_2_out21), .out22(demultiplexer_2_out22), .out23(demultiplexer_2_out23),
    .out24(demultiplexer_2_out24), .out25(demultiplexer_2_out25), .out26(demultiplexer_2_out26),
    .out27(demultiplexer_2_out27), .out28(demultiplexer_2_out28), .out29(demultiplexer_2_out29),
    .out30(demultiplexer_2_out30), .out31(demultiplexer_2_out31), .in(R2), .sel(ADR2));  // open: en
  and and_1 (and_1_out, demultiplexer_1_out0, R);
  and and_2 (and_2_out, demultiplexer_1_out1, R);
  and and_3 (and_3_out, demultiplexer_1_out2, R);
  and and_4 (and_4_out, demultiplexer_1_out3, R);
  and and_5 (and_5_out, demultiplexer_1_out4, R);
  and and_6 (and_6_out, demultiplexer_1_out5, R);
  and and_7 (and_7_out, demultiplexer_1_out6, R);
  and and_8 (and_8_out, demultiplexer_1_out7, R);
  and and_9 (and_9_out, demultiplexer_1_out8, R);
  and and_10 (and_10_out, demultiplexer_1_out9, R);
  and and_11 (and_11_out, demultiplexer_1_out10, R);
  and and_12 (and_12_out, demultiplexer_1_out11, R);
  and and_13 (and_13_out, demultiplexer_1_out12, R);
  and and_14 (and_14_out, demultiplexer_1_out13, R);
  and and_15 (and_15_out, demultiplexer_1_out14, R);
  and and_16 (and_16_out, demultiplexer_1_out15, R);
  and and_17 (and_17_out, demultiplexer_1_out16, R);
  and and_18 (and_18_out, demultiplexer_1_out17, R);
  and and_19 (and_19_out, demultiplexer_1_out18, R);
  and and_20 (and_20_out, demultiplexer_1_out19, R);
  and and_21 (and_21_out, demultiplexer_1_out20, R);
  and and_22 (and_22_out, demultiplexer_1_out21, R);
  and and_23 (and_23_out, demultiplexer_1_out22, R);
  and and_24 (and_24_out, demultiplexer_1_out23, R);
  and and_25 (and_25_out, demultiplexer_1_out24, R);
  and and_26 (and_26_out, demultiplexer_1_out25, R);
  and and_27 (and_27_out, demultiplexer_1_out26, R);
  and and_28 (and_28_out, demultiplexer_1_out27, R);
  and and_29 (and_29_out, demultiplexer_1_out28, R);
  and and_30 (and_30_out, demultiplexer_1_out29, R);
  and and_31 (and_31_out, demultiplexer_1_out30, R);
  and and_32 (and_32_out, demultiplexer_1_out31, R);
  and and_33 (and_33_out, W, demultiplexer_1_out0);
  and and_34 (and_34_out, W, demultiplexer_1_out1);
  and and_35 (and_35_out, W, demultiplexer_1_out2);
  and and_36 (and_36_out, W, demultiplexer_1_out3);
  and and_37 (and_37_out, W, demultiplexer_1_out4);
  and and_38 (and_38_out, W, demultiplexer_1_out5);
  and and_39 (and_39_out, W, demultiplexer_1_out6);
  and and_40 (and_40_out, W, demultiplexer_1_out7);
  and and_41 (and_41_out, W, demultiplexer_1_out8);
  and and_42 (and_42_out, W, demultiplexer_1_out9);
  and and_43 (and_43_out, W, demultiplexer_1_out10);
  and and_44 (and_44_out, W, demultiplexer_1_out11);
  and and_45 (and_45_out, W, demultiplexer_1_out12);
  and and_46 (and_46_out, W, demultiplexer_1_out13);
  and and_47 (and_47_out, W, demultiplexer_1_out14);
  and and_48 (and_48_out, W, demultiplexer_1_out15);
  and and_49 (and_49_out, W, demultiplexer_1_out16);
  and and_50 (and_50_out, W, demultiplexer_1_out17);
  and and_51 (and_51_out, W, demultiplexer_1_out18);
  and and_52 (and_52_out, W, demultiplexer_1_out19);
  and and_53 (and_53_out, W, demultiplexer_1_out20);
  and and_54 (and_54_out, W, demultiplexer_1_out21);
  and and_55 (and_55_out, W, demultiplexer_1_out22);
  and and_56 (and_56_out, W, demultiplexer_1_out23);
  and and_57 (and_57_out, W, demultiplexer_1_out24);
  and and_58 (and_58_out, W, demultiplexer_1_out25);
  and and_59 (and_59_out, W, demultiplexer_1_out26);
  and and_60 (and_60_out, W, demultiplexer_1_out27);
  and and_61 (and_61_out, W, demultiplexer_1_out28);
  and and_62 (and_62_out, W, demultiplexer_1_out29);
  and and_63 (and_63_out, W, demultiplexer_1_out30);
  and and_64 (and_64_out, W, demultiplexer_1_out31);
  Cell1 cell1_1 (
    .W(and_33_out), .IN(IN), .OUT(cell1_1_out), .CLK(CLK), .R(and_1_out), .OUT2(cell1_1_out2),
    .R2(demultiplexer_2_out0));
  Cell1 cell1_2 (
    .W(and_34_out), .IN(IN), .OUT(cell1_2_out), .CLK(CLK), .R(and_2_out), .OUT2(cell1_2_out2),
    .R2(demultiplexer_2_out1));
  Cell1 cell1_3 (
    .W(and_35_out), .IN(IN), .OUT(cell1_3_out), .CLK(CLK), .R(and_3_out), .OUT2(cell1_3_out2),
    .R2(demultiplexer_2_out2));
  Cell1 cell1_4 (
    .W(and_36_out), .IN(IN), .OUT(cell1_4_out), .CLK(CLK), .R(and_4_out), .OUT2(cell1_4_out2),
    .R2(demultiplexer_2_out3));
  Cell1 cell1_5 (
    .W(and_37_out), .IN(IN), .OUT(cell1_5_out), .CLK(CLK), .R(and_5_out), .OUT2(cell1_5_out2),
    .R2(demultiplexer_2_out4));
  Cell1 cell1_6 (
    .W(and_38_out), .IN(IN), .OUT(cell1_6_out), .CLK(CLK), .R(and_6_out), .OUT2(cell1_6_out2),
    .R2(demultiplexer_2_out5));
  Cell1 cell1_7 (
    .W(and_39_out), .IN(IN), .OUT(cell1_7_out), .CLK(CLK), .R(and_7_out), .OUT2(cell1_7_out2),
    .R2(demultiplexer_2_out6));
  Cell1 cell1_8 (
    .W(and_40_out), .IN(IN), .OUT(cell1_8_out), .CLK(CLK), .R(and_8_out), .OUT2(cell1_8_out2),
    .R2(demultiplexer_2_out7));
  Cell1 cell1_9 (
    .W(and_41_out), .IN(IN), .OUT(cell1_9_out), .CLK(CLK), .R(and_9_out), .OUT2(cell1_9_out2),
    .R2(demultiplexer_2_out8));
  Cell1 cell1_10 (
    .W(and_42_out), .IN(IN), .OUT(cell1_10_out), .CLK(CLK), .R(and_10_out), .OUT2(cell1_10_out2),
    .R2(demultiplexer_2_out9));
  Cell1 cell1_11 (
    .W(and_43_out), .IN(IN), .OUT(cell1_11_out), .CLK(CLK), .R(and_11_out), .OUT2(cell1_11_out2),
    .R2(demultiplexer_2_out10));
  Cell1 cell1_12 (
    .W(and_44_out), .IN(IN), .OUT(cell1_12_out), .CLK(CLK), .R(and_12_out), .OUT2(cell1_12_out2),
    .R2(demultiplexer_2_out11));
  Cell1 cell1_13 (
    .W(and_45_out), .IN(IN), .OUT(cell1_13_out), .CLK(CLK), .R(and_13_out), .OUT2(cell1_13_out2),
    .R2(demultiplexer_2_out12));
  Cell1 cell1_14 (
    .W(and_46_out), .IN(IN), .OUT(cell1_14_out), .CLK(CLK), .R(and_14_out), .OUT2(cell1_14_out2),
    .R2(demultiplexer_2_out13));
  Cell1 cell1_15 (
    .W(and_47_out), .IN(IN), .OUT(cell1_15_out), .CLK(CLK), .R(and_15_out), .OUT2(cell1_15_out2),
    .R2(demultiplexer_2_out14));
  Cell1 cell1_16 (
    .W(and_48_out), .IN(IN), .OUT(cell1_16_out), .CLK(CLK), .R(and_16_out), .OUT2(cell1_16_out2),
    .R2(demultiplexer_2_out15));
  Cell1 cell1_17 (
    .W(and_49_out), .IN(IN), .OUT(cell1_17_out), .CLK(CLK), .R(and_17_out), .OUT2(cell1_17_out2),
    .R2(demultiplexer_2_out16));
  Cell1 cell1_18 (
    .W(and_50_out), .IN(IN), .OUT(cell1_18_out), .CLK(CLK), .R(and_18_out), .OUT2(cell1_18_out2),
    .R2(demultiplexer_2_out17));
  Cell1 cell1_19 (
    .W(and_51_out), .IN(IN), .OUT(cell1_19_out), .CLK(CLK), .R(and_19_out), .OUT2(cell1_19_out2),
    .R2(demultiplexer_2_out18));
  Cell1 cell1_20 (
    .W(and_52_out), .IN(IN), .OUT(cell1_20_out), .CLK(CLK), .R(and_20_out), .OUT2(cell1_20_out2),
    .R2(demultiplexer_2_out19));
  Cell1 cell1_21 (
    .W(and_53_out), .IN(IN), .OUT(cell1_21_out), .CLK(CLK), .R(and_21_out), .OUT2(cell1_21_out2),
    .R2(demultiplexer_2_out20));
  Cell1 cell1_22 (
    .W(and_54_out), .IN(IN), .OUT(cell1_22_out), .CLK(CLK), .R(and_22_out), .OUT2(cell1_22_out2),
    .R2(demultiplexer_2_out21));
  Cell1 cell1_23 (
    .W(and_55_out), .IN(IN), .OUT(cell1_23_out), .CLK(CLK), .R(and_23_out), .OUT2(cell1_23_out2),
    .R2(demultiplexer_2_out22));
  Cell1 cell1_24 (
    .W(and_56_out), .IN(IN), .OUT(cell1_24_out), .CLK(CLK), .R(and_24_out), .OUT2(cell1_24_out2),
    .R2(demultiplexer_2_out23));
  Cell1 cell1_25 (
    .W(and_57_out), .IN(IN), .OUT(cell1_25_out), .CLK(CLK), .R(and_25_out), .OUT2(cell1_25_out2),
    .R2(demultiplexer_2_out24));
  Cell1 cell1_26 (
    .W(and_58_out), .IN(IN), .OUT(cell1_26_out), .CLK(CLK), .R(and_26_out), .OUT2(cell1_26_out2),
    .R2(demultiplexer_2_out25));
  Cell1 cell1_27 (
    .W(and_59_out), .IN(IN), .OUT(cell1_27_out), .CLK(CLK), .R(and_27_out), .OUT2(cell1_27_out2),
    .R2(demultiplexer_2_out26));
  Cell1 cell1_28 (
    .W(and_60_out), .IN(IN), .OUT(cell1_28_out), .CLK(CLK), .R(and_28_out), .OUT2(cell1_28_out2),
    .R2(demultiplexer_2_out27));
  Cell1 cell1_29 (
    .W(and_61_out), .IN(IN), .OUT(cell1_29_out), .CLK(CLK), .R(and_29_out), .OUT2(cell1_29_out2),
    .R2(demultiplexer_2_out28));
  Cell1 cell1_30 (
    .W(and_62_out), .IN(IN), .OUT(cell1_30_out), .CLK(CLK), .R(and_30_out), .OUT2(cell1_30_out2),
    .R2(demultiplexer_2_out29));
  Cell1 cell1_31 (
    .W(and_63_out), .IN(IN), .OUT(cell1_31_out), .CLK(CLK), .R(and_31_out), .OUT2(cell1_31_out2),
    .R2(demultiplexer_2_out30));
  Cell1 cell1_32 (
    .W(and_64_out), .IN(IN), .OUT(cell1_32_out), .CLK(CLK), .R(and_32_out), .OUT2(cell1_32_out2),
    .R2(demultiplexer_2_out31));
  assign OUT2 = cell1_32_out2 | cell1_31_out2 | cell1_30_out2 | cell1_29_out2 | cell1_28_out2 | cell1_27_out2 | cell1_26_out2 | cell1_25_out2 | cell1_24_out2 | cell1_23_out2 | cell1_22_out2 | cell1_21_out2 | cell1_20_out2 | cell1_19_out2 | cell1_18_out2 | cell1_17_out2 | cell1_16_out2 | cell1_15_out2 | cell1_14_out2 | cell1_13_out2 | cell1_12_out2 | cell1_11_out2 | cell1_10_out2 | cell1_9_out2 | cell1_8_out2 | cell1_7_out2 | cell1_6_out2 | cell1_5_out2 | cell1_4_out2 | cell1_3_out2 | cell1_2_out2 | cell1_1_out2;  // OR_Gate or_1, 5 bits wide
  assign OUT = cell1_1_out | cell1_2_out | cell1_3_out | cell1_4_out | cell1_5_out | cell1_6_out | cell1_7_out | cell1_8_out | cell1_9_out | cell1_10_out | cell1_11_out | cell1_12_out | cell1_13_out | cell1_14_out | cell1_15_out | cell1_16_out | cell1_17_out | cell1_18_out | cell1_19_out | cell1_20_out | cell1_21_out | cell1_22_out | cell1_23_out | cell1_24_out | cell1_25_out | cell1_26_out | cell1_27_out | cell1_28_out | cell1_29_out | cell1_30_out | cell1_31_out | cell1_32_out;  // OR_Gate or_2, 5 bits wide
endmodule

module XCM_CPU (
  input  CLK,
  input  [4:0] INPUT_0,
  input  [4:0] INPUT_1,
  input  [4:0] INPUT_2,
  input  [4:0] INPUT_3,
  input  [14:0] IR_DATA,
  output [9:0] IR_ADR,
  output [11:0] DISPLAY
);

  wire demultiplexer_1_out0, demultiplexer_1_out1, demultiplexer_1_out2, demultiplexer_1_out3,
       demultiplexer_1_out4, demultiplexer_1_out5, demultiplexer_1_out6, demultiplexer_1_out7,
       demultiplexer_1_out8, demultiplexer_1_out9, demultiplexer_1_out10, demultiplexer_1_out11,
       demultiplexer_1_out12, demultiplexer_1_out13, demultiplexer_1_out14, demultiplexer_1_out15,
       demultiplexer_1_out16, ir_cmpbc_1_cmp_out, ir_cmprc_1_cmp_out, ir_cmprr_1_cmp_out, ir_neqbc_1_cmp_out,
       ir_neqrc_1_cmp_out, ir_neqrr_1_cmp_out, SKP_out;
  wire [4:0] ir_bcpy_1_rob_in, ir_cmpbc_1_rob_in, ir_neqbc_1_rob_in, or_2_out, ram5_1_out, ram5_1_out2,
       rob_1_out;
  wire [11:0] ir_drwc_1_display, ir_drwr_1_display, ir_ersc_1_display, ir_ersr_1_display;
  wire [17:0] ir_bcpy_1_ram_in, ir_cmprc_1_ram_in, ir_cmprr_1_ram_in, ir_cpy_1_ram_in, ir_dec_1_ram_in,
       ir_drwr_1_ram_in, ir_ersr_1_ram_in, ir_inc_1_ram_in, ir_neqrc_1_ram_in, ir_neqrr_1_ram_in,
       ir_set_1_ram_in, RAM_IN_out;

  Demultiplexer #(.select(5)) demultiplexer_1 (
    .out0(demultiplexer_1_out0), .out1(demultiplexer_1_out1), .out2(demultiplexer_1_out2),
    .out3(demultiplexer_1_out3), .out4(demultiplexer_1_out4), .out5(demultiplexer_1_out5),
    .out6(demultiplexer_1_out6), .out7(demultiplexer_1_out7), .out8(demultiplexer_1_out8),
    .out9(demultiplexer_1_out9), .out10(demultiplexer_1_out10), .out11(demultiplexer_1_out11),
    .out12(demultiplexer_1_out12), .out13(demultiplexer_1_out13), .out14(demultiplexer_1_out14),
    .out15(demultiplexer_1_out15), .out16(demultiplexer_1_out16), .in(CLK), .sel(IR_DATA[4:0]));  // open: out17, out18, out19, out20, out21, out22, out23, out24, out25, out26, out27, out28, out29, out30, out31, en
  IL il_1 (.JMP(demultiplexer_1_out0), .L(IR_DATA[9:5]), .P(IR_DATA[14:10]), .CLK(CLK), .ROM_IN(IR_ADR), .SKP(SKP_out));
  IR_SET ir_set_1 (.SEL(demultiplexer_1_out3), .REG(IR_DATA[9:5]), .DATA(IR_DATA[14:10]), .RAM_IN(ir_set_1_ram_in));
  IR_INC ir_inc_1 (
    .REG_ADR(IR_DATA[9:5]), .RAM_OUT({ram5_1_out2, ram5_1_out}), .RAM_IN(ir_inc_1_ram_in),
    .SEL(demultiplexer_1_out5));
  IR_DEC ir_dec_1 (
    .SEL(demultiplexer_1_out6), .REG_ADR(IR_DATA[9:5]), .RAM_OUT({ram5_1_out2, ram5_1_out}),
    .RAM_IN(ir_dec_1_ram_in));
  IR_DRWC ir_drwc_1 (.SEL(demultiplexer_1_out8), .X(IR_DATA[9:5]), .Y(IR_DATA[14:10]), .DISPLAY(ir_drwc_1_display));
  IR_ERSC ir_ersc_1 (.SEL(demultiplexer_1_out10), .DISPLAY(ir_ersc_1_display), .X(IR_DATA[9:5]), .Y(IR_DATA[14:10]));
  IR_CMPRC ir_cmprc_1 (
    .SEL(demultiplexer_1_out1), .REG_ADR(IR_DATA[9:5]), .CON(IR_DATA[14:10]),
    .RAM_OUT({ram5_1_out2, ram5_1_out}), .RAM_IN(ir_cmprc_1_ram_in), .CMP_OUT(ir_cmprc_1_cmp_out));
  IR_NEQRC ir_neqrc_1 (
    .SEL(demultiplexer_1_out2), .REG_ADR(IR_DATA[9:5]), .CON(IR_DATA[14:10]),
    .RAM_OUT({ram5_1_out2, ram5_1_out}), .RAM_IN(ir_neqrc_1_ram_in), .CMP_OUT(ir_neqrc_1_cmp_out));
  IR_CPY ir_cpy_1 (
    .SEL(demultiplexer_1_out4), .REG_SRC(IR_DATA[9:5]), .RAM_OUT({ram5_1_out2, ram5_1_out}),
    .REG_DST(IR_DATA[14:10]), .RAM_IN(ir_cpy_1_ram_in));
  IR_DRWR ir_drwr_1 (
    .SEL(demultiplexer_1_out7), .RAM_OUT({ram5_1_out2, ram5_1_out}), .ADR_X(IR_DATA[9:5]),
    .ADR_Y(IR_DATA[14:10]), .DISPLAY(ir_drwr_1_display), .RAM_IN(ir_drwr_1_ram_in));
  IR_ERSR ir_ersr_1 (
    .SEL(demultiplexer_1_out9), .DISPLAY(ir_ersr_1_display), .RAM_OUT({ram5_1_out2, ram5_1_out}),
    .RAM_IN(ir_ersr_1_ram_in), .ADR_X(IR_DATA[9:5]), .ADR_Y(IR_DATA[14:10]));
  IR_BCPY ir_bcpy_1 (
    .SEL(demultiplexer_1_out11), .REG_ADR(IR_DATA[14:10]), .BUF_DATA(rob_1_out), .BUF_ADR(IR_DATA[9:5]),
    .RAM_IN(ir_bcpy_1_ram_in), .ROB_IN(ir_bcpy_1_rob_in));
  IR_CMPBC ir_cmpbc_1 (
    .SEL(demultiplexer_1_out12), .BUF_ADR(IR_DATA[9:5]), .CON(IR_DATA[14:10]), .ROB_OUT(rob_1_out),
    .ROB_IN(ir_cmpbc_1_rob_in), .CMP_OUT(ir_cmpbc_1_cmp_out));
  IR_NEQBC ir_neqbc_1 (
    .SEL(demultiplexer_1_out13), .BUF_ADR(IR_DATA[9:5]), .CON(IR_DATA[14:10]), .ROB_OUT(rob_1_out),
    .ROB_IN(ir_neqbc_1_rob_in), .CMP_OUT(ir_neqbc_1_cmp_out));
  IR_CMPRR ir_cmprr_1 (
    .SEL(demultiplexer_1_out14), .REG_ADR(IR_DATA[9:5]), .REG_ADR2(IR_DATA[14:10]),
    .RAM_OUT({ram5_1_out2, ram5_1_out}), .RAM_IN(ir_cmprr_1_ram_in), .CMP_OUT(ir_cmprr_1_cmp_out));
  IR_NEQRR ir_neqrr_1 (
    .SEL(demultiplexer_1_out15), .REG_ADR(IR_DATA[9:5]), .REG_ADR2(IR_DATA[14:10]),
    .RAM_OUT({ram5_1_out2, ram5_1_out}), .RAM_IN(ir_neqrr_1_ram_in), .CMP_OUT(ir_neqrr_1_cmp_out));
  or SKP (SKP_out, ir_cmprc_1_cmp_out, ir_neqrc_1_cmp_out, ir_neqbc_1_cmp_out, ir_cmpbc_1_cmp_out, ir_neqrr_1_cmp_out, ir_cmprr_1_cmp_out);
  assign DISPLAY = ir_drwr_1_display | ir_drwc_1_display | ir_ersr_1_display | ir_ersc_1_display;  // OR_Gate or_1, 12 bits wide
  assign RAM_IN_out = ir_neqrc_1_ram_in | ir_neqrr_1_ram_in | ir_dec_1_ram_in | ir_cmprr_1_ram_in | ir_cmprc_1_ram_in | ir_cpy_1_ram_in | ir_ersr_1_ram_in | ir_inc_1_ram_in | ir_drwr_1_ram_in | ir_set_1_ram_in | ir_bcpy_1_ram_in;  // OR_Gate RAM_IN, 18 bits wide
  RAM5 ram5_1 (
    .SEL(1'b1), .ADR(RAM_IN_out[7:3]), .OUT(ram5_1_out), .R(RAM_IN_out[0]), .W(RAM_IN_out[2]),
    .IN(RAM_IN_out[12:8]), .CLK(CLK), .ADR2(RAM_IN_out[17:13]), .R2(RAM_IN_out[1]), .OUT2(ram5_1_out2));
  ROB rob_1 (.B0(INPUT_0), .B1(INPUT_1), .B2(INPUT_2), .B3(INPUT_3), .ADR(or_2_out), .OUT(rob_1_out), .CLK(CLK));
  assign or_2_out = ir_neqbc_1_rob_in | ir_bcpy_1_rob_in | ir_cmpbc_1_rob_in;  // OR_Gate or_2, 5 bits wide
endmodule

module ROB (
  input  CLK,
  input  [4:0] B0,
  input  [4:0] B1,
  input  [4:0] B2,
  input  [4:0] B3,
  input  [4:0] ADR,
  output [4:0] OUT
);

  wire demultiplexer_1_out0, demultiplexer_1_out1, demultiplexer_1_out2, demultiplexer_1_out3;
  wire [4:0] cell1_1_out, cell1_2_out, cell1_3_out, cell1_4_out;

  Demultiplexer #(.select(5)) demultiplexer_1 (
    .out0(demultiplexer_1_out0), .out1(demultiplexer_1_out1), .out2(demultiplexer_1_out2),
    .out3(demultiplexer_1_out3), .in(1'b1), .sel(ADR));  // open: out4, out5, out6, out7, out8, out9, out10, out11, out12, out13, out14, out15, out16, out17, out18, out19, out20, out21, out22, out23, out24, out25, out26, out27, out28, out29, out30, out31, en
  Cell1 cell1_1 (.W(1'b1), .IN(B0), .OUT(cell1_1_out), .CLK(CLK), .R(demultiplexer_1_out0));  // open: OUT2, R2
  Cell1 cell1_2 (.W(1'b1), .IN(B1), .OUT(cell1_2_out), .CLK(CLK), .R(demultiplexer_1_out1));  // open: OUT2, R2
  Cell1 cell1_3 (.W(1'b1), .IN(B2), .OUT(cell1_3_out), .CLK(CLK), .R(demultiplexer_1_out2));  // open: OUT2, R2
  Cell1 cell1_4 (.W(1'b1), .IN(B3), .OUT(cell1_4_out), .CLK(CLK), .R(demultiplexer_1_out3));  // open: OUT2, R2
  assign OUT = cell1_1_out | cell1_2_out | cell1_3_out | cell1_4_out;  // OR_Gate or_1, 5 bits wide
endmodule

module IL (
  input  JMP,
  input  [4:0] P,
  input  [4:0] L,
  input  SKP,
  input  CLK,
  output [9:0] ROM_IN
);

  wire demultiplexer_1_out0, demultiplexer_1_out1, demultiplexer_2_out0, demultiplexer_2_out1,
       demultiplexer_3_out0, demultiplexer_3_out1, demultiplexer_4_out0, demultiplexer_4_out1,
       demultiplexer_5_out0, demultiplexer_5_out1, demultiplexer_6_out0, demultiplexer_6_out1,
       demultiplexer_7_out0, demultiplexer_7_out1, demultiplexer_8_out0, demultiplexer_8_out1,
       demultiplexer_9_out0, demultiplexer_9_out1, demultiplexer_10_out0, demultiplexer_10_out1,
       multiplexer_1_out, multiplexer_2_out, multiplexer_3_out, multiplexer_4_out, multiplexer_5_out,
       multiplexer_6_out, multiplexer_7_out, multiplexer_8_out, multiplexer_9_out, multiplexer_10_out,
       multiplexer_11_out, multiplexer_12_out, multiplexer_13_out, multiplexer_14_out, multiplexer_15_out,
       multiplexer_16_out, multiplexer_17_out, multiplexer_18_out, multiplexer_19_out, multiplexer_20_out;
  wire [9:0] inc10_1_out, inc10_2_out;

  Multiplexer multiplexer_1 (.in0(inc10_1_out[0]), .in1(L[0]), .out(multiplexer_1_out), .sel(JMP));  // open: en
  Multiplexer multiplexer_2 (.in0(inc10_1_out[1]), .in1(L[1]), .out(multiplexer_2_out), .sel(JMP));  // open: en
  Multiplexer multiplexer_3 (.in0(inc10_1_out[2]), .in1(L[2]), .out(multiplexer_3_out), .sel(JMP));  // open: en
  Multiplexer multiplexer_4 (.in0(inc10_1_out[3]), .in1(L[3]), .out(multiplexer_4_out), .sel(JMP));  // open: en
  Multiplexer multiplexer_5 (.in0(inc10_1_out[4]), .in1(L[4]), .out(multiplexer_5_out), .sel(JMP));  // open: en
  Multiplexer multiplexer_6 (.in0(inc10_1_out[5]), .in1(P[0]), .out(multiplexer_6_out), .sel(JMP));  // open: en
  Multiplexer multiplexer_7 (.in0(inc10_1_out[6]), .in1(P[1]), .out(multiplexer_7_out), .sel(JMP));  // open: en
  Multiplexer multiplexer_8 (.in0(inc10_1_out[7]), .in1(P[2]), .out(multiplexer_8_out), .sel(JMP));  // open: en
  Multiplexer multiplexer_9 (.in0(inc10_1_out[8]), .in1(P[3]), .out(multiplexer_9_out), .sel(JMP));  // open: en
  Multiplexer multiplexer_10 (.in0(inc10_1_out[9]), .in1(P[4]), .out(multiplexer_10_out), .sel(JMP));  // open: en
  Demultiplexer demultiplexer_1 (
    .out0(demultiplexer_1_out0), .out1(demultiplexer_1_out1), .in(1'b1), .sel(multiplexer_11_out));  // open: en
  Multiplexer multiplexer_11 (
    .in0(multiplexer_1_out), .in1(inc10_2_out[0]), .out(multiplexer_11_out), .sel(SKP));  // open: en
  Demultiplexer demultiplexer_2 (
    .out0(demultiplexer_2_out0), .out1(demultiplexer_2_out1), .in(1'b1), .sel(multiplexer_12_out));  // open: en
  Multiplexer multiplexer_12 (
    .in0(multiplexer_2_out), .in1(inc10_2_out[1]), .out(multiplexer_12_out), .sel(SKP));  // open: en
  Demultiplexer demultiplexer_3 (
    .out0(demultiplexer_3_out0), .out1(demultiplexer_3_out1), .in(1'b1), .sel(multiplexer_13_out));  // open: en
  Multiplexer multiplexer_13 (
    .in0(multiplexer_3_out), .in1(inc10_2_out[2]), .out(multiplexer_13_out), .sel(SKP));  // open: en
  Demultiplexer demultiplexer_4 (
    .out0(demultiplexer_4_out0), .out1(demultiplexer_4_out1), .in(1'b1), .sel(multiplexer_14_out));  // open: en
  Multiplexer multiplexer_14 (
    .in0(multiplexer_4_out), .in1(inc10_2_out[3]), .out(multiplexer_14_out), .sel(SKP));  // open: en
  Demultiplexer demultiplexer_5 (
    .out0(demultiplexer_5_out0), .out1(demultiplexer_5_out1), .in(1'b1), .sel(multiplexer_15_out));  // open: en
  Multiplexer multiplexer_15 (
    .in0(multiplexer_5_out), .in1(inc10_2_out[4]), .out(multiplexer_15_out), .sel(SKP));  // open: en
  Demultiplexer demultiplexer_6 (
    .out0(demultiplexer_6_out0), .out1(demultiplexer_6_out1), .in(1'b1), .sel(multiplexer_16_out));  // open: en
  Multiplexer multiplexer_16 (
    .in0(multiplexer_6_out), .in1(inc10_2_out[5]), .out(multiplexer_16_out), .sel(SKP));  // open: en
  Demultiplexer demultiplexer_7 (
    .out0(demultiplexer_7_out0), .out1(demultiplexer_7_out1), .in(1'b1), .sel(multiplexer_17_out));  // open: en
  Multiplexer multiplexer_17 (
    .in0(multiplexer_7_out), .in1(inc10_2_out[6]), .out(multiplexer_17_out), .sel(SKP));  // open: en
  Demultiplexer demultiplexer_8 (
    .out0(demultiplexer_8_out0), .out1(demultiplexer_8_out1), .in(1'b1), .sel(multiplexer_18_out));  // open: en
  Multiplexer multiplexer_18 (
    .in0(multiplexer_8_out), .in1(inc10_2_out[7]), .out(multiplexer_18_out), .sel(SKP));  // open: en
  Demultiplexer demultiplexer_9 (
    .out0(demultiplexer_9_out0), .out1(demultiplexer_9_out1), .in(1'b1), .sel(multiplexer_19_out));  // open: en
  Multiplexer multiplexer_19 (
    .in0(multiplexer_9_out), .in1(inc10_2_out[8]), .out(multiplexer_19_out), .sel(SKP));  // open: en
  Demultiplexer demultiplexer_10 (
    .out0(demultiplexer_10_out0), .out1(demultiplexer_10_out1), .in(1'b1), .sel(multiplexer_20_out));  // open: en
  Multiplexer multiplexer_20 (
    .in0(multiplexer_10_out), .in1(inc10_2_out[9]), .out(multiplexer_20_out), .sel(SKP));  // open: en
  S_R_Flip_Flop #(.trigger("falling")) s_r_ff_1 (
    .S(demultiplexer_1_out1), .clk(CLK), .R(demultiplexer_1_out0), .Q(ROM_IN[0]));  // open: Qn, preset, reset, en
  S_R_Flip_Flop #(.trigger("falling")) s_r_ff_2 (
    .S(demultiplexer_2_out1), .clk(CLK), .R(demultiplexer_2_out0), .Q(ROM_IN[1]));  // open: Qn, preset, reset, en
  S_R_Flip_Flop #(.trigger("falling")) s_r_ff_3 (
    .S(demultiplexer_3_out1), .clk(CLK), .R(demultiplexer_3_out0), .Q(ROM_IN[2]));  // open: Qn, preset, reset, en
  S_R_Flip_Flop #(.trigger("falling")) s_r_ff_4 (
    .S(demultiplexer_4_out1), .clk(CLK), .R(demultiplexer_4_out0), .Q(ROM_IN[3]));  // open: Qn, preset, reset, en
  S_R_Flip_Flop #(.trigger("falling")) s_r_ff_5 (
    .S(demultiplexer_5_out1), .clk(CLK), .R(demultiplexer_5_out0), .Q(ROM_IN[4]));  // open: Qn, preset, reset, en
  S_R_Flip_Flop #(.trigger("falling")) s_r_ff_6 (
    .S(demultiplexer_6_out1), .clk(CLK), .R(demultiplexer_6_out0), .Q(ROM_IN[5]));  // open: Qn, preset, reset, en
  S_R_Flip_Flop #(.trigger("falling")) s_r_ff_7 (
    .S(demultiplexer_7_out1), .clk(CLK), .R(demultiplexer_7_out0), .Q(ROM_IN[6]));  // open: Qn, preset, reset, en
  S_R_Flip_Flop #(.trigger("falling")) s_r_ff_8 (
    .S(demultiplexer_8_out1), .clk(CLK), .R(demultiplexer_8_out0), .Q(ROM_IN[7]));  // open: Qn, preset, reset, en
  S_R_Flip_Flop #(.trigger("falling")) s_r_ff_9 (
    .S(demultiplexer_9_out1), .clk(CLK), .R(demultiplexer_9_out0), .Q(ROM_IN[8]));  // open: Qn, preset, reset, en
  S_R_Flip_Flop #(.trigger("falling")) s_r_ff_10 (
    .S(demultiplexer_10_out1), .clk(CLK), .R(demultiplexer_10_out0), .Q(ROM_IN[9]));  // open: Qn, preset, reset, en
  INC10 inc10_1 (.IN(ROM_IN), .OUT(inc10_1_out));
  INC10 inc10_2 (.IN(inc10_1_out), .OUT(inc10_2_out));
endmodule

module IR_DRWC (
  input  SEL,
  input  [4:0] X,
  input  [4:0] Y,
  output [11:0] DISPLAY
);

  assign DISPLAY = {12{SEL}} & {Y, X, 1'b1, SEL};  // AND_Gate and_1, 12 bits wide
endmodule

module IR_ERSC (
  input  SEL,
  input  [4:0] X,
  input  [4:0] Y,
  output [11:0] DISPLAY
);

  assign DISPLAY = {12{SEL}} & {Y, X, 1'b0, SEL};  // AND_Gate and_1, 12 bits wide
endmodule

module IR_SET (
  input  SEL,
  input  [4:0] REG,
  input  [4:0] DATA,
  output [17:0] RAM_IN
);

  assign RAM_IN = {18{SEL}} & {{5{1'b0}}, DATA, REG, 3'b100};  // AND_Gate and_1, 18 bits wide

  // Notes on the sheet:
  //   R R2 W ADR IN ADR2
endmodule

module IR_DRWR (
  input  SEL,
  input  [9:0] RAM_OUT,
  input  [4:0] ADR_X,
  input  [4:0] ADR_Y,
  output [11:0] DISPLAY,
  output [17:0] RAM_IN
);

  assign DISPLAY = {12{SEL}} & {RAM_OUT, 1'b1, SEL};  // AND_Gate and_1, 12 bits wide
  assign RAM_IN = {18{SEL}} & {ADR_Y, {5{1'b0}}, ADR_X, 3'b011};  // AND_Gate and_2, 18 bits wide

  // Notes on the sheet:
  //   R R2 W ADR IN ADR2
endmodule

module IR_INC (
  input  SEL,
  input  [4:0] REG_ADR,
  input  [9:0] RAM_OUT,
  output [17:0] RAM_IN
);

  wire and_1_out, and_2_out, and_3_out;
  wire [4:0] not_1_out;

  not not_1 (not_1_out[0], RAM_OUT[0]);
  and and_1 (and_1_out, RAM_OUT[0], RAM_OUT[1]);
  xor xor_1 (not_1_out[1], RAM_OUT[0], RAM_OUT[1]);
  xor xor_2 (not_1_out[2], and_1_out, RAM_OUT[2]);
  and and_2 (and_2_out, and_1_out, RAM_OUT[2]);
  xor xor_3 (not_1_out[3], and_2_out, RAM_OUT[3]);
  and and_3 (and_3_out, and_2_out, RAM_OUT[3]);
  xor xor_4 (not_1_out[4], and_3_out, RAM_OUT[4]);
  assign RAM_IN = {18{SEL}} & {{5{1'b0}}, not_1_out, REG_ADR, 3'b101};  // AND_Gate and_4, 18 bits wide

  // Notes on the sheet:
  //   R R2 W ADR IN ADR2
endmodule

module IR_ERSR (
  input  SEL,
  input  [9:0] RAM_OUT,
  input  [4:0] ADR_X,
  input  [4:0] ADR_Y,
  output [11:0] DISPLAY,
  output [17:0] RAM_IN
);

  assign DISPLAY = {12{SEL}} & {RAM_OUT, 1'b0, SEL};  // AND_Gate and_1, 12 bits wide
  assign RAM_IN = {18{SEL}} & {ADR_Y, {5{1'b0}}, ADR_X, 3'b011};  // AND_Gate and_2, 18 bits wide

  // Notes on the sheet:
  //   R R2 W ADR IN ADR2
endmodule

module INC10 (
  input  [9:0] IN,
  output [9:0] OUT
);

  wire and_1_out, and_2_out, and_3_out, and_4_out, and_5_out, and_6_out, and_7_out, and_8_out;

  not not_1 (OUT[0], IN[0]);
  xor xor_1 (OUT[1], IN[0], IN[1]);
  and and_1 (and_1_out, IN[0], IN[1]);
  xor xor_2 (OUT[2], and_1_out, IN[2]);
  and and_2 (and_2_out, and_1_out, IN[2]);
  and and_3 (and_3_out, and_2_out, IN[3]);
  xor xor_3 (OUT[3], and_2_out, IN[3]);
  xor xor_4 (OUT[4], and_3_out, IN[4]);
  and and_4 (and_4_out, and_3_out, IN[4]);
  xor xor_5 (OUT[5], and_4_out, IN[5]);
  and and_5 (and_5_out, and_4_out, IN[5]);
  xor xor_6 (OUT[6], and_5_out, IN[6]);
  and and_6 (and_6_out, and_5_out, IN[6]);
  xor xor_7 (OUT[7], and_6_out, IN[7]);
  and and_7 (and_7_out, and_6_out, IN[7]);
  xor xor_8 (OUT[8], and_7_out, IN[8]);
  and and_8 (and_8_out, and_7_out, IN[8]);
  xor xor_9 (OUT[9], and_8_out, IN[9]);
endmodule

module IR_CPY (
  input  SEL,
  input  [4:0] REG_DST,
  input  [9:0] RAM_OUT,
  input  [4:0] REG_SRC,
  output [17:0] RAM_IN
);

  assign RAM_IN = {18{SEL}} & {REG_SRC, RAM_OUT[9:5], REG_DST, 3'b110};  // AND_Gate and_1, 18 bits wide

  // Notes on the sheet:
  //   R R2 W ADR IN ADR2
endmodule

module IR_CMPRC (
  input  SEL,
  input  [4:0] REG_ADR,
  input  [4:0] CON,
  input  [9:0] RAM_OUT,
  output [17:0] RAM_IN,
  output CMP_OUT
);

  wire and_1_out;
  wire [4:0] xnor_1_out;

  assign xnor_1_out = ~(CON ^ RAM_OUT[4:0]);  // XNOR_Gate xnor_1, 5 bits wide
  and and_1 (and_1_out, xnor_1_out[0], xnor_1_out[1], xnor_1_out[2], xnor_1_out[3], xnor_1_out[4]);
  assign RAM_IN = {18{SEL}} & {{10{1'b0}}, REG_ADR, 3'b001};  // AND_Gate and_2, 18 bits wide
  and and_3 (CMP_OUT, SEL, ~and_1_out);  // AND_Gate

  // Notes on the sheet:
  //   R R2 W ADR IN ADR2
endmodule

module IR_CMPRR (
  input  SEL,
  input  [4:0] REG_ADR,
  input  [4:0] REG_ADR2,
  input  [9:0] RAM_OUT,
  output [17:0] RAM_IN,
  output CMP_OUT
);

  wire and_1_out;
  wire [4:0] xnor_1_out;

  assign xnor_1_out = ~(RAM_OUT[9:5] ^ RAM_OUT[4:0]);  // XNOR_Gate xnor_1, 5 bits wide
  and and_1 (and_1_out, xnor_1_out[0], xnor_1_out[1], xnor_1_out[2], xnor_1_out[3], xnor_1_out[4]);
  assign RAM_IN = {18{SEL}} & {REG_ADR2, {5{1'b0}}, REG_ADR, 3'b011};  // AND_Gate and_2, 18 bits wide
  and and_3 (CMP_OUT, SEL, ~and_1_out);  // AND_Gate

  // Notes on the sheet:
  //   R R2 W ADR IN ADR2
endmodule

module IR_DEC (
  input  SEL,
  input  [4:0] REG_ADR,
  input  [9:0] RAM_OUT,
  output [17:0] RAM_IN
);

  wire and_1_out, and_2_out, and_3_out, not_2_out, not_3_out, not_4_out, not_5_out;
  wire [4:0] not_1_out;

  not not_1 (not_1_out[0], RAM_OUT[0]);
  not not_2 (not_2_out, RAM_OUT[0]);
  xor xor_1 (not_1_out[1], not_2_out, RAM_OUT[1]);
  and and_1 (and_1_out, not_2_out, not_3_out);
  not not_3 (not_3_out, RAM_OUT[1]);
  not not_4 (not_4_out, RAM_OUT[2]);
  xor xor_2 (not_1_out[2], and_1_out, RAM_OUT[2]);
  and and_2 (and_2_out, and_1_out, not_4_out);
  not not_5 (not_5_out, RAM_OUT[3]);
  xor xor_3 (not_1_out[3], and_2_out, RAM_OUT[3]);
  and and_3 (and_3_out, and_2_out, not_5_out);
  xor xor_4 (not_1_out[4], and_3_out, RAM_OUT[4]);
  assign RAM_IN = {18{SEL}} & {{5{1'b0}}, not_1_out, REG_ADR, 3'b101};  // AND_Gate and_4, 18 bits wide

  // Notes on the sheet:
  //   R R2 W ADR IN ADR2
endmodule

module IR_NEQRC (
  input  SEL,
  input  [4:0] REG_ADR,
  input  [4:0] CON,
  input  [9:0] RAM_OUT,
  output [17:0] RAM_IN,
  output CMP_OUT
);

  wire and_1_out;
  wire [4:0] xnor_1_out;

  assign xnor_1_out = ~(CON ^ RAM_OUT[4:0]);  // XNOR_Gate xnor_1, 5 bits wide
  and and_1 (and_1_out, xnor_1_out[0], xnor_1_out[1], xnor_1_out[2], xnor_1_out[3], xnor_1_out[4]);
  assign RAM_IN = {18{SEL}} & {{10{1'b0}}, REG_ADR, 3'b001};  // AND_Gate and_2, 18 bits wide
  and and_3 (CMP_OUT, SEL, and_1_out);

  // Notes on the sheet:
  //   R R2 W ADR IN ADR2
endmodule

module IR_NEQRR (
  input  SEL,
  input  [4:0] REG_ADR,
  input  [4:0] REG_ADR2,
  input  [9:0] RAM_OUT,
  output [17:0] RAM_IN,
  output CMP_OUT
);

  wire and_1_out;
  wire [4:0] xnor_1_out;

  assign xnor_1_out = ~(RAM_OUT[9:5] ^ RAM_OUT[4:0]);  // XNOR_Gate xnor_1, 5 bits wide
  and and_1 (and_1_out, xnor_1_out[0], xnor_1_out[1], xnor_1_out[2], xnor_1_out[3], xnor_1_out[4]);
  assign RAM_IN = {18{SEL}} & {REG_ADR2, {5{1'b0}}, REG_ADR, 3'b011};  // AND_Gate and_2, 18 bits wide
  and and_3 (CMP_OUT, SEL, and_1_out);

  // Notes on the sheet:
  //   R R2 W ADR IN ADR2
endmodule

module IR_CMPBC (
  input  SEL,
  input  [4:0] BUF_ADR,
  input  [4:0] CON,
  input  [4:0] ROB_OUT,
  output [4:0] ROB_IN,
  output CMP_OUT
);

  wire and_1_out;
  wire [4:0] xnor_1_out;

  assign xnor_1_out = ~(CON ^ ROB_OUT);  // XNOR_Gate xnor_1, 5 bits wide
  and and_1 (and_1_out, xnor_1_out[0], xnor_1_out[1], xnor_1_out[2], xnor_1_out[3], xnor_1_out[4]);
  assign ROB_IN = {5{SEL}} & BUF_ADR;  // AND_Gate and_2, 5 bits wide
  and and_3 (CMP_OUT, SEL, ~and_1_out);  // AND_Gate
endmodule

module IR_NEQBC (
  input  SEL,
  input  [4:0] BUF_ADR,
  input  [4:0] CON,
  input  [4:0] ROB_OUT,
  output [4:0] ROB_IN,
  output CMP_OUT
);

  wire and_1_out;
  wire [4:0] xnor_1_out;

  assign xnor_1_out = ~(CON ^ ROB_OUT);  // XNOR_Gate xnor_1, 5 bits wide
  and and_1 (and_1_out, xnor_1_out[0], xnor_1_out[1], xnor_1_out[2], xnor_1_out[3], xnor_1_out[4]);
  assign ROB_IN = {5{SEL}} & BUF_ADR;  // AND_Gate and_2, 5 bits wide
  and and_3 (CMP_OUT, SEL, and_1_out);
endmodule

module IR_BCPY (
  input  SEL,
  input  [4:0] REG_ADR,
  input  [4:0] BUF_DATA,
  input  [4:0] BUF_ADR,
  output [17:0] RAM_IN,
  output [4:0] ROB_IN
);

  assign ROB_IN = {5{SEL}} & BUF_ADR;  // AND_Gate and_1, 5 bits wide
  assign RAM_IN = {18{SEL}} & {{5{1'b0}}, BUF_DATA, REG_ADR, 3'b100};  // AND_Gate and_2, 18 bits wide

  // Notes on the sheet:
  //   R R2 W ADR IN ADR2
endmodule
